// Logisim project Clase_1_Logica_Secuencial.circ as structural Verilog: 5 circuits, main circuit main
module main (
  input  Set,
  input  Entrada_D,
  input  Reset,
  input  [1:0] in_4,
  input  [1:0] in_5,
  input  [1:0] in_6,
  input  [1:0] in_7,
  input  [6:0] in_8,
  input  [3:0] in_9,
  input  [3:0] in_10,
  input  [6:0] in_11,
  output Salida_Q,
  output Salida__Q,
  output [7:0] out_14,
  output [7:0] out_15,
  output [7:0] out_16,
  output [7:0] out_17,
  output [7:0] out_18,
  output [7:0] out_19
);

  wire button_1_out, button_2_out, button_3_out, clock_1_out, clock_2_out, clock_3_out, clock_4_out,
       clock_6_out;
  wire [6:0] keyboard_1_data;
  wire [7:0] multiplexer_1_out;

  Keyboard keyboard_1 (.clk(clock_1_out), .data(keyboard_1_data));  // open: re, clr, avail
  Clock clock_1 (.out(clock_1_out));
  Clock clock_2 (.out(clock_2_out));
  Tablero tablero_1 (
    .Clock(clock_4_out), .Reset(button_2_out), .Write_Add(in_6), .Dato(multiplexer_1_out), .Dir_a(in_4),
    .Dir_b(in_5), .Open_B(out_15), .Open_A(out_14));
  Clock clock_3 (.out(clock_3_out));
  Contador contador_1 (.in_1(clock_3_out), .in_2(button_1_out));
  D_Flip_Flop d_ff_1 (.D(Entrada_D), .clk(clock_2_out), .Q(Salida_Q), .Qn(Salida__Q), .preset(Set), .reset(Reset));
  Clock clock_4 (.out(clock_4_out));
  Clock clock_5 ();  // open: out
  Button button_1 (.out(button_1_out));
  Detector_Rango detector_rango_1 (.Techo(in_8), .Teclado(keyboard_1_data), .Piso(in_11));
  Button button_2 (.out(button_2_out));
  Multiplexer #(.select(2), .width(8)) multiplexer_1 (
    .in0(out_17), .in1(out_18), .in2(out_19), .in3(out_16), .out(multiplexer_1_out), .sel(in_7));
  assign out_17 = out_15 & out_14;  // AND_Gate and_1, 8 bits wide
  Clock clock_6 (.out(clock_6_out));
  assign out_18 = out_15 | out_14;  // OR_Gate or_1, 8 bits wide
  Contador_confi contador_confi_1 (.CLK(clock_6_out), .Reset(button_3_out), .Start(in_9), .Step(in_10));
  Button button_3 (.out(button_3_out));
  assign out_19 = ~out_15;  // NOT_Gate not_1, 8 bits wide
  Adder adder_1 (.a(out_14), .b(out_15), .out(out_16));  // open: cin, cout

  // Notes on the sheet:
  //   Clock
endmodule

module Tablero (
  input  [1:0] Write_Add,
  input  [1:0] Dir_a,
  input  [1:0] Dir_b,
  input  [7:0] Dato,
  input  Clock,
  input  Reset,
  output [7:0] Open_A,
  output [7:0] Open_B
);

  wire decoder_1_out0, decoder_1_out1, decoder_1_out2, decoder_1_out3;
  wire [3:0] binary_to_bcd_converter_1_p2, binary_to_bcd_converter_1_p3, binary_to_bcd_converter_1_p4,
       binary_to_bcd_converter_2_p2, binary_to_bcd_converter_2_p3, binary_to_bcd_converter_2_p4,
       binary_to_bcd_converter_3_p2, binary_to_bcd_converter_3_p3, binary_to_bcd_converter_3_p4,
       binary_to_bcd_converter_4_p2, binary_to_bcd_converter_4_p3, binary_to_bcd_converter_4_p4, R0_q,
       R0_q_2, R1_q, R1_q_2, R2_q, R2_q_2, R3_q, R3_q_2;

  Decoder #(.select(2)) decoder_1 (
    .out0(decoder_1_out0), .out1(decoder_1_out1), .out2(decoder_1_out2), .out3(decoder_1_out3),
    .sel(Write_Add));  // open: en
  Register R0 (.D(Dato), .en(decoder_1_out0), .clk(Clock), .Q({R0_q_2, R0_q}), .clr(Reset));
  Register R1 (.D(Dato), .en(decoder_1_out1), .clk(Clock), .Q({R1_q_2, R1_q}), .clr(Reset));
  Register R2 (.D(Dato), .en(decoder_1_out2), .clk(Clock), .Q({R2_q_2, R2_q}), .clr(Reset));
  Register R3 (.D(Dato), .en(decoder_1_out3), .clk(Clock), .Q({R3_q_2, R3_q}), .clr(Reset));
  Hex_Digit_Display R0_2 (.value(R0_q_2));  // open: dp
  Hex_Digit_Display R0_1 (.value(R0_q));  // open: dp
  Hex_Digit_Display R1_2 (.value(R1_q_2));  // open: dp
  Hex_Digit_Display R1_1 (.value(R1_q));  // open: dp
  Hex_Digit_Display R2_2 (.value(R2_q_2));  // open: dp
  Hex_Digit_Display R2_1 (.value(R2_q));  // open: dp
  Hex_Digit_Display R3_2 (.value(R3_q_2));  // open: dp
  Hex_Digit_Display R3_1 (.value(R3_q));  // open: dp
  Hex_Digit_Display R0_DEC_2 (.value(binary_to_bcd_converter_1_p2));  // open: dp
  // Binary_to_BCD_converter #(.binvalue(8)) binary_to_bcd_converter_1: pin names not known; wires that end beside it: {R0_q_2, R0_q}, binary_to_bcd_converter_1_p2, binary_to_bcd_converter_1_p3, binary_to_bcd_converter_1_p4
  Hex_Digit_Display R1_DEC_2 (.value(binary_to_bcd_converter_2_p2));  // open: dp
  // Binary_to_BCD_converter #(.binvalue(8)) binary_to_bcd_converter_2: pin names not known; wires that end beside it: {R1_q_2, R1_q}, binary_to_bcd_converter_2_p2, binary_to_bcd_converter_2_p3, binary_to_bcd_converter_2_p4
  Hex_Digit_Display R2_DEC_2 (.value(binary_to_bcd_converter_3_p2));  // open: dp
  // Binary_to_BCD_converter #(.binvalue(8)) binary_to_bcd_converter_3: pin names not known; wires that end beside it: {R2_q_2, R2_q}, binary_to_bcd_converter_3_p2, binary_to_bcd_converter_3_p3, binary_to_bcd_converter_3_p4
  Hex_Digit_Display R3_DEC_2 (.value(binary_to_bcd_converter_4_p2));  // open: dp
  // Binary_to_BCD_converter #(.binvalue(8)) binary_to_bcd_converter_4: pin names not known; wires that end beside it: {R3_q_2, R3_q}, binary_to_bcd_converter_4_p2, binary_to_bcd_converter_4_p3, binary_to_bcd_converter_4_p4
  Hex_Digit_Display R0_DEC_1 (.value(binary_to_bcd_converter_1_p3));  // open: dp
  Hex_Digit_Display R1_DEC_1 (.value(binary_to_bcd_converter_2_p3));  // open: dp
  Hex_Digit_Display R2_DEC_1 (.value(binary_to_bcd_converter_3_p3));  // open: dp
  Hex_Digit_Display R3_DEC_1 (.value(binary_to_bcd_converter_4_p3));  // open: dp
  Hex_Digit_Display R0_DEC_0 (.value(binary_to_bcd_converter_1_p4));  // open: dp
  Hex_Digit_Display R1_DEC_0 (.value(binary_to_bcd_converter_2_p4));  // open: dp
  Hex_Digit_Display R2_DEC_0 (.value(binary_to_bcd_converter_3_p4));  // open: dp
  Hex_Digit_Display R3_DEC_0 (.value(binary_to_bcd_converter_4_p4));  // open: dp
  Multiplexer #(.select(2), .width(8)) multiplexer_1 (
    .in0({R0_q_2, R0_q}), .in1({R1_q_2, R1_q}), .in2({R2_q_2, R2_q}), .in3({R3_q_2, R3_q}), .out(Open_A),
    .sel(Dir_a));
  Multiplexer #(.select(2), .width(8)) multiplexer_2 (
    .in0({R0_q_2, R0_q}), .in1({R1_q_2, R1_q}), .in2({R2_q_2, R2_q}), .in3({R3_q_2, R3_q}), .out(Open_B),
    .sel(Dir_b));
endmodule

module Contador (
  input  in_1,
  input  in_2
);

  wire and_1_out, or_1_out;
  wire [3:0] adder_1_out, register_1_q;

  Register #(.width(4)) register_1 (.D(adder_1_out), .en(1'b1), .clk(in_1), .Q(register_1_q), .clr(or_1_out));
  or or_1 (or_1_out, in_2, and_1_out);
  Adder #(.width(4)) adder_1 (.a(4'b0001), .b(register_1_q), .out(adder_1_out));  // open: cin, cout
  Hex_Digit_Display Num (.value(register_1_q));  // open: dp
  and and_1 (and_1_out, register_1_q[0], register_1_q[1], register_1_q[2], register_1_q[3]);
endmodule

module Detector_Rango (
  input  [6:0] Techo,
  input  [6:0] Teclado,
  input  [6:0] Piso
);

  wire and_1_out, comparator_1_lt, comparator_2_gt;

  Comparator #(.width(7)) comparator_1 (.a(Techo), .b(Teclado), .lt(comparator_1_lt));  // open: gt, eq
  Comparator #(.width(7)) comparator_2 (.a(Teclado), .b(Piso), .gt(comparator_2_gt));  // open: eq, lt
  and and_1 (and_1_out, comparator_1_lt, comparator_2_gt);
  LED indicador (.in(and_1_out));
endmodule

module Contador_confi (
  input  [3:0] Step,
  input  [3:0] Start,
  input  CLK,
  input  Reset
);

  wire and_1_out, d_ff_1_q, or_1_out, or_2_out;
  wire [3:0] multiplexer_1_out, register_1_q, Sumatoria;

  D_Flip_Flop d_ff_1 (.D(1'b1), .clk(CLK), .Q(d_ff_1_q), .reset(Reset));  // open: Qn, preset
  or or_1 (or_1_out, d_ff_1_q, 1'b0);
  Register #(.width(4)) register_1 (.D(multiplexer_1_out), .en(1'b1), .clk(CLK), .Q(register_1_q), .clr(or_2_out));
  Multiplexer #(.width(4)) multiplexer_1 (.in0(Start), .in1(Sumatoria), .out(multiplexer_1_out), .sel(or_1_out));
  or or_2 (or_2_out, Reset, and_1_out);
  Adder #(.width(4)) adder_1 (.a(Step), .b(register_1_q), .out(Sumatoria));  // open: cin, cout
  Hex_Digit_Display Num (.value(register_1_q));  // open: dp
  and and_1 (and_1_out, register_1_q[0], register_1_q[1], register_1_q[2], register_1_q[3]);
endmodule
