// Logisim project 20213714_LAB_1.circ as structural Verilog: 6 circuits, main circuit main
module main (
  input  [2:0] in_1,
  input  [3:0] in_2,
  input  [3:0] in_3,
  input  in_4,
  input  [3:0] in_5
);

  wire pregunta_2_1_b1, pregunta_2_1_b2, pregunta_2_1_g, pregunta_2_1_g2, pregunta_2_1_r1, pregunta_2_1_r2;
  wire [3:0] binary_to_bcd_converter_1_p2, binary_to_bcd_converter_1_p3, binary_to_bcd_converter_1_p4;
  wire [8:0] a_out_3;
  wire [13:0] bit_extender_1_out;

  Pregunta_3 a (.A(in_2), .B(in_3), .out_3(a_out_3));
  Pregunta_2 pregunta_2_1 (
    .Entrada(in_1), .G(pregunta_2_1_g), .B2(pregunta_2_1_b2), .R2(pregunta_2_1_r2), .G2(pregunta_2_1_g2),
    .B1(pregunta_2_1_b1), .R1(pregunta_2_1_r1));
  // RGBLED rgbled_1: pin names not known; wires that end beside it: pregunta_2_1_r1, pregunta_2_1_g, pregunta_2_1_b1
  // RGBLED rgbled_2: pin names not known; wires that end beside it: pregunta_2_1_r2, pregunta_2_1_g2, pregunta_2_1_b2
  assign bit_extender_1_out = {{5{1'b0}}, a_out_3};  // Bit_Extender bit_extender_1
  Hex_Digit_Display hex_digit_display_1 (.value(binary_to_bcd_converter_1_p2));  // open: dp
  // Binary_to_BCD_converter binary_to_bcd_converter_1: pin names not known; wires that end beside it: a_out_3, binary_to_bcd_converter_1_p2, binary_to_bcd_converter_1_p3, binary_to_bcd_converter_1_p4
  // Buzzer #(.vol_width(4)) buzzer_1: pin names not known; wires that end beside it: in_4, in_5, bit_extender_1_out
  Hex_Digit_Display hex_digit_display_2 (.value(binary_to_bcd_converter_1_p3));  // open: dp
  Hex_Digit_Display hex_digit_display_3 (.value(binary_to_bcd_converter_1_p4));  // open: dp

  // Notes on the sheet:
  //   Pregunta 2
  //   Pregunta 3
endmodule

module Pregunta_1 (
  input  Entrada,
  input  [1:0] Selector,
  input  Entradas,
  input  in_4,
  input  in_5,
  input  in_6,
  input  in_7,
  output Salidas,
  output out_9,
  output out_10,
  output out_11,
  output Valida_Salida,
  output [1:0] Salida,
  output out_14
);

  Decoder #(.select(2)) decoder_1 (
    .out0(Salidas), .out1(out_9), .out2(out_10), .out3(out_11), .sel(Selector), .en(Entrada));
  Priority_Encoder #(.select(2)) priority_encoder_1 (
    .in0(Entradas), .in1(in_4), .in2(in_5), .in3(in_6), .out(Salida), .gs(out_14), .en_out(Valida_Salida),
    .en_in(in_7));

  // Notes on the sheet:
  //   Decoder
  //   Encoder
  //   Habilitador
  //   Group Select
  //   Salida elegida
endmodule

module Pregunta_2 (
  input  [2:0] Entrada,
  output B1,
  output R1,
  output G,
  output B2,
  output R2,
  output G2
);

  wire and_1_out, and_2_out, and_3_out, and_4_out, and_5_out, and_6_out, and_7_out, and_8_out, and_9_out,
       and_10_out, and_11_out, and_12_out, and_13_out, and_14_out, and_15_out, and_16_out, and_17_out,
       not_1_out, not_2_out, not_3_out;

  not not_1 (not_1_out, Entrada[2]);
  not not_2 (not_2_out, Entrada[1]);
  not not_3 (not_3_out, Entrada[0]);
  and and_1 (and_1_out, not_1_out, not_2_out, not_3_out);
  and and_2 (and_2_out, not_1_out, Entrada[1], Entrada[0]);
  and and_3 (and_3_out, Entrada[2], not_2_out, Entrada[0]);
  and and_4 (and_4_out, Entrada[2], Entrada[1], not_3_out);
  and and_5 (and_5_out, not_2_out, Entrada[0]);
  and and_6 (and_6_out, Entrada[2], not_3_out);
  and and_7 (and_7_out, not_1_out, Entrada[1]);
  and and_8 (and_8_out, Entrada[2], not_3_out);
  and and_9 (and_9_out, not_1_out, Entrada[1]);
  and and_10 (and_10_out, Entrada[2], not_2_out, not_3_out);
  and and_11 (and_11_out, Entrada[1], Entrada[0]);
  and and_12 (and_12_out, not_2_out, Entrada[0]);
  and and_13 (and_13_out, Entrada[2], not_2_out);
  and and_14 (and_14_out, Entrada[2], Entrada[0]);
  and and_15 (and_15_out, not_1_out, not_2_out, not_3_out);
  and and_16 (and_16_out, Entrada[1], Entrada[0]);
  and and_17 (and_17_out, Entrada[2], Entrada[0]);
  or or_1 (G, and_1_out, and_2_out, and_3_out, and_4_out);
  or or_2 (R1, and_5_out, and_6_out);
  or or_3 (B1, and_7_out, and_8_out);
  or or_4 (G2, and_9_out, and_10_out, and_11_out);
  or or_5 (R2, and_12_out, and_13_out, and_14_out);
  or or_6 (B2, and_15_out, and_16_out, and_17_out);
endmodule

module Pregunta_3 (
  input  [3:0] A,
  input  [3:0] B,
  output [8:0] out_3
);

  wire comparator_1_eq, comparator_1_gt, comparator_1_lt;
  wire [1:0] priority_encoder_1_out;
  wire [8:0] adder_1_out, adder_2_out, adder_3_out, bit_extender_1_out, bit_extender_2_out, multiplier_1_out,
       multiplier_2_out, multiplier_3_out, multiplier_4_out, multiplier_5_out, multiplier_6_out;

  assign bit_extender_1_out = {{5{1'b0}}, A};  // Bit_Extender bit_extender_1
  assign bit_extender_2_out = {{5{1'b0}}, B};  // Bit_Extender bit_extender_2
  Comparator #(.width(4)) comparator_1 (.a(A), .b(B), .gt(comparator_1_gt), .eq(comparator_1_eq), .lt(comparator_1_lt));
  Priority_Encoder #(.select(2)) priority_encoder_1 (
    .in0(comparator_1_gt), .in1(comparator_1_eq), .in2(comparator_1_lt), .out(priority_encoder_1_out));  // open: in3, gs, en_out, en_in
  Multiplier #(.width(9)) multiplier_1 (.a(9'h8), .b(bit_extender_1_out), .out(multiplier_1_out));  // open: cin, cout
  Multiplier #(.width(9)) multiplier_2 (.a(9'h3), .b(bit_extender_2_out), .out(multiplier_2_out));  // open: cin, cout
  Multiplier #(.width(9)) multiplier_3 (.a(9'h5), .b(bit_extender_1_out), .out(multiplier_3_out));  // open: cin, cout
  Multiplier #(.width(9)) multiplier_4 (.a(9'h3), .b(bit_extender_2_out), .out(multiplier_4_out));  // open: cin, cout
  Multiplier #(.width(9)) multiplier_5 (.a(9'h3), .b(bit_extender_1_out), .out(multiplier_5_out));  // open: cin, cout
  Multiplier #(.width(9)) multiplier_6 (.a(9'h9), .b(bit_extender_2_out), .out(multiplier_6_out));  // open: cin, cout
  Adder #(.width(9)) adder_1 (.a(multiplier_1_out), .b(multiplier_2_out), .out(adder_1_out));  // open: cin, cout
  Adder #(.width(9)) adder_2 (.a(multiplier_3_out), .b(multiplier_4_out), .out(adder_2_out));  // open: cin, cout
  Adder #(.width(9)) adder_3 (.a(multiplier_5_out), .b(multiplier_6_out), .out(adder_3_out));  // open: cin, cout
  Multiplexer #(.select(2), .width(9)) multiplexer_1 (
    .in0(adder_1_out), .in1(adder_2_out), .in2(adder_3_out), .out(out_3), .sel(priority_encoder_1_out));  // open: in3

  // Notes on the sheet:
  //   PARTE a
endmodule

module Pregunta3_b (
  input  [3:0] in_1,
  input  [3:0] in_2,
  output [8:0] out_3
);

  wire comparator_1_eq, comparator_1_gt, comparator_1_lt;
  wire [1:0] priority_encoder_1_out;
  wire [8:0] adder_1_out, adder_2_out, adder_3_out, bit_extender_1_out, bit_extender_2_out, undriven,
       undriven_2, undriven_3, undriven_4, undriven_5, undriven_6;

  assign bit_extender_1_out = {{5{1'b0}}, in_1};  // Bit_Extender bit_extender_1
  assign bit_extender_2_out = {{5{1'b0}}, in_2};  // Bit_Extender bit_extender_2
  Comparator #(.width(4)) comparator_1 (
    .a(in_1), .b(in_2), .gt(comparator_1_gt), .eq(comparator_1_eq), .lt(comparator_1_lt));
  Priority_Encoder #(.select(2)) priority_encoder_1 (
    .in0(comparator_1_gt), .in1(comparator_1_eq), .in2(comparator_1_lt), .out(priority_encoder_1_out));  // open: in3, gs, en_out, en_in
  Adder #(.width(9)) adder_1 (.a(undriven), .b(undriven_4), .out(adder_1_out));  // open: cin, cout
  Adder #(.width(9)) adder_2 (.a(undriven_2), .b(undriven_5), .out(adder_2_out));  // open: cin, cout
  Adder #(.width(9)) adder_3 (.a(undriven_3), .b(undriven_6), .out(adder_3_out));  // open: cin, cout
  Multiplexer #(.select(2), .width(9)) multiplexer_1 (
    .in0(adder_1_out), .in1(adder_2_out), .in2(adder_3_out), .out(out_3), .sel(priority_encoder_1_out));  // open: in3

  // Notes on the sheet:
  //   PARTE B
endmodule

module Multiplicador_ParteB (
  input  [8:0] Constante,
  input  [8:0] Numero
);
endmodule
