// Logisim project ROSA CRISTINA LA CRUZ MUSAYON - LAB3_plantilla.circ as structural Verilog: 3 circuits, main circuit Preg_1
module Preg_1 (
);

  wire clock_1_out, reset;
  wire [1:0] dir_b;
  wire [2:0] dir_A, operation;
  wire [7:0] adder_1_out, and_1_out, multiplexer_1_out, multiplexer_2_out, multiplexer_3_out, not_1_out,
       or_1_out, register_bank_8_1_ope_a, register_bank_8_1_ope_b, register_bank_8_1_r0o,
       register_bank_8_1_r1o, register_bank_8_1_r2o, register_bank_8_1_r3o, register_bank_8_1_r4o,
       register_bank_8_1_r5o, register_bank_8_1_r6o, register_bank_8_1_r7o;

  DotMatrix #(.matrixcols(8), .matrixrows(8)) dotmatrix_1 (
    .col0(register_bank_8_1_r7o), .col1(register_bank_8_1_r6o), .col2(register_bank_8_1_r5o),
    .col3(register_bank_8_1_r4o), .col4(register_bank_8_1_r3o), .col5(register_bank_8_1_r2o),
    .col6(register_bank_8_1_r1o), .col7(register_bank_8_1_r0o));
  Clock clock_1 (.out(clock_1_out));
  register_bank_8 register_bank_8_1 (
    .clock_reg(clock_1_out), .reset_reg(reset), .dir_DATO(dir_A), .dato(multiplexer_1_out), .dir_A(dir_A),
    .dir_B(dir_b), .ope_A(register_bank_8_1_ope_a), .R7o(register_bank_8_1_r7o), .R6o(register_bank_8_1_r6o),
    .R5o(register_bank_8_1_r5o), .R4o(register_bank_8_1_r4o), .R3o(register_bank_8_1_r3o),
    .R2o(register_bank_8_1_r2o), .R1o(register_bank_8_1_r1o), .R0o(register_bank_8_1_r0o),
    .ope_B(register_bank_8_1_ope_b));  // open: enable
  Multiplexer #(.select(3), .width(8)) multiplexer_1 (
    .in0(and_1_out), .in1(or_1_out), .in2(adder_1_out), .in3(register_bank_8_1_ope_b),
    .in4(multiplexer_2_out), .in5(multiplexer_3_out), .out(multiplexer_1_out), .sel(operation));  // open: in6, in7
  assign and_1_out = register_bank_8_1_ope_a & register_bank_8_1_ope_b;  // AND_Gate and_1, 8 bits wide
  assign or_1_out = register_bank_8_1_ope_a | register_bank_8_1_ope_b;  // OR_Gate or_1, 8 bits wide
  ROM rom_1 (.data({operation, dir_A, dir_b}));  // open: addr
  Adder adder_1 (.a(register_bank_8_1_ope_b), .b(register_bank_8_1_ope_a), .out(adder_1_out));  // open: cin, cout
  Button button_1 (.out(reset));
  Multiplexer #(.select(2), .width(8)) multiplexer_2 (
    .in0({register_bank_8_1_ope_a[6:0], 1'b0}), .in1({1'b0, register_bank_8_1_ope_a[7:1]}),
    .in2({register_bank_8_1_ope_a[6:0], register_bank_8_1_ope_a[7]}),
    .in3({register_bank_8_1_ope_a[0], register_bank_8_1_ope_a[7:1]}), .out(multiplexer_2_out), .sel(dir_b));
  assign not_1_out = ~register_bank_8_1_ope_a;  // NOT_Gate not_1, 8 bits wide
  Multiplexer #(.select(2), .width(8)) multiplexer_3 (
    .in0(not_1_out), .in1({8{1'b0}}), .in2({8{1'b1}}),
    .in3({register_bank_8_1_ope_a[3:0], register_bank_8_1_ope_a[7:4]}), .out(multiplexer_3_out), .sel(dir_b));

  // Other names for the same wires on the sheet: step_5[4:0] = {dir_A, dir_b}
endmodule

module register_bank_8 (
  input  [2:0] dir_DATO,
  input  enable,
  input  [2:0] dir_A,
  input  [1:0] dir_B,
  input  [7:0] dato,
  input  clock_reg,
  input  reset_reg,
  output [7:0] ope_A,
  output [7:0] ope_B,
  output [7:0] R7o,
  output [7:0] R6o,
  output [7:0] R5o,
  output [7:0] R4o,
  output [7:0] R3o,
  output [7:0] R2o,
  output [7:0] R1o,
  output [7:0] R0o
);

  wire decoder_1_out0, decoder_1_out1, decoder_1_out2, decoder_1_out3, decoder_1_out4, decoder_1_out5,
       decoder_1_out6, decoder_1_out7;
  wire [3:0] binary_to_bcd_converter_1_p2, binary_to_bcd_converter_1_p3, binary_to_bcd_converter_1_p4,
       binary_to_bcd_converter_2_p2, binary_to_bcd_converter_2_p3, binary_to_bcd_converter_2_p4,
       binary_to_bcd_converter_3_p2, binary_to_bcd_converter_3_p3, binary_to_bcd_converter_3_p4,
       binary_to_bcd_converter_4_p2, binary_to_bcd_converter_4_p3, binary_to_bcd_converter_4_p4,
       binary_to_bcd_converter_5_p2, binary_to_bcd_converter_5_p3, binary_to_bcd_converter_5_p4,
       binary_to_bcd_converter_6_p2, binary_to_bcd_converter_6_p3, binary_to_bcd_converter_6_p4,
       binary_to_bcd_converter_7_p2, binary_to_bcd_converter_7_p3, binary_to_bcd_converter_7_p4,
       binary_to_bcd_converter_8_p2, binary_to_bcd_converter_8_p3, binary_to_bcd_converter_8_p4;

  Decoder #(.select(3)) decoder_1 (
    .out0(decoder_1_out0), .out1(decoder_1_out1), .out2(decoder_1_out2), .out3(decoder_1_out3),
    .out4(decoder_1_out4), .out5(decoder_1_out5), .out6(decoder_1_out6), .out7(decoder_1_out7),
    .sel(dir_DATO), .en(enable));
  Register register_1 (.D(dato), .en(decoder_1_out7), .clk(clock_reg), .Q(R7o), .clr(reset_reg));
  Register register_2 (.D(dato), .en(decoder_1_out6), .clk(clock_reg), .Q(R6o), .clr(reset_reg));
  Register register_3 (.D(dato), .en(decoder_1_out5), .clk(clock_reg), .Q(R5o), .clr(reset_reg));
  Register register_4 (.D(dato), .en(decoder_1_out4), .clk(clock_reg), .Q(R4o), .clr(reset_reg));
  Register R3 (.D(dato), .en(decoder_1_out3), .clk(clock_reg), .Q(R3o), .clr(reset_reg));
  Register R2 (.D(dato), .en(decoder_1_out2), .clk(clock_reg), .Q(R2o), .clr(reset_reg));
  Register R1 (.D(dato), .en(decoder_1_out1), .clk(clock_reg), .Q(R1o), .clr(reset_reg));
  Register R0 (.D(dato), .en(decoder_1_out0), .clk(clock_reg), .Q(R0o), .clr(reset_reg));
  Hex_Digit_Display R7_h_H (.value(R7o[7:4]));  // open: dp
  Hex_Digit_Display R6_h_H (.value(R6o[7:4]));  // open: dp
  Hex_Digit_Display R5_h_H (.value(R5o[7:4]));  // open: dp
  Hex_Digit_Display R4_h_H (.value(R4o[7:4]));  // open: dp
  Hex_Digit_Display R3_hex_H (.value(R3o[7:4]));  // open: dp
  Hex_Digit_Display R2_hex_H (.value(R2o[7:4]));  // open: dp
  Hex_Digit_Display R1_hex_H (.value(R1o[7:4]));  // open: dp
  Hex_Digit_Display R0_hex_H (.value(R0o[7:4]));  // open: dp
  Hex_Digit_Display R7_h_L (.value(R7o[3:0]));  // open: dp
  Hex_Digit_Display R6_h_L (.value(R6o[3:0]));  // open: dp
  Hex_Digit_Display R5_h_L (.value(R5o[3:0]));  // open: dp
  Hex_Digit_Display R4_h_L (.value(R4o[3:0]));  // open: dp
  Hex_Digit_Display R3_hex_L (.value(R3o[3:0]));  // open: dp
  Hex_Digit_Display R2_hex_L (.value(R2o[3:0]));  // open: dp
  Hex_Digit_Display R1_hex_L (.value(R1o[3:0]));  // open: dp
  Hex_Digit_Display R0_hex_L (.value(R0o[3:0]));  // open: dp
  Hex_Digit_Display R7d2 (.value(binary_to_bcd_converter_1_p2));  // open: dp
  // Binary_to_BCD_converter #(.binvalue(8)) binary_to_bcd_converter_1: pin names not known; wires that end beside it: R7o, binary_to_bcd_converter_1_p2, binary_to_bcd_converter_1_p3, binary_to_bcd_converter_1_p4
  Hex_Digit_Display R6d2 (.value(binary_to_bcd_converter_2_p2));  // open: dp
  // Binary_to_BCD_converter #(.binvalue(8)) binary_to_bcd_converter_2: pin names not known; wires that end beside it: R6o, binary_to_bcd_converter_2_p2, binary_to_bcd_converter_2_p3, binary_to_bcd_converter_2_p4
  Hex_Digit_Display R5d2 (.value(binary_to_bcd_converter_3_p2));  // open: dp
  // Binary_to_BCD_converter #(.binvalue(8)) binary_to_bcd_converter_3: pin names not known; wires that end beside it: R5o, binary_to_bcd_converter_3_p2, binary_to_bcd_converter_3_p3, binary_to_bcd_converter_3_p4
  Hex_Digit_Display R4d2 (.value(binary_to_bcd_converter_4_p2));  // open: dp
  // Binary_to_BCD_converter #(.binvalue(8)) binary_to_bcd_converter_4: pin names not known; wires that end beside it: R4o, binary_to_bcd_converter_4_p2, binary_to_bcd_converter_4_p3, binary_to_bcd_converter_4_p4
  Hex_Digit_Display R3dec2 (.value(binary_to_bcd_converter_5_p2));  // open: dp
  // Binary_to_BCD_converter #(.binvalue(8)) binary_to_bcd_converter_5: pin names not known; wires that end beside it: R3o, binary_to_bcd_converter_5_p2, binary_to_bcd_converter_5_p3, binary_to_bcd_converter_5_p4
  Hex_Digit_Display R2dec2 (.value(binary_to_bcd_converter_6_p2));  // open: dp
  // Binary_to_BCD_converter #(.binvalue(8)) binary_to_bcd_converter_6: pin names not known; wires that end beside it: R2o, binary_to_bcd_converter_6_p2, binary_to_bcd_converter_6_p3, binary_to_bcd_converter_6_p4
  Hex_Digit_Display R1dec2 (.value(binary_to_bcd_converter_7_p2));  // open: dp
  // Binary_to_BCD_converter #(.binvalue(8)) binary_to_bcd_converter_7: pin names not known; wires that end beside it: R1o, binary_to_bcd_converter_7_p2, binary_to_bcd_converter_7_p3, binary_to_bcd_converter_7_p4
  Hex_Digit_Display R0dec2 (.value(binary_to_bcd_converter_8_p2));  // open: dp
  // Binary_to_BCD_converter #(.binvalue(8)) binary_to_bcd_converter_8: pin names not known; wires that end beside it: R0o, binary_to_bcd_converter_8_p2, binary_to_bcd_converter_8_p3, binary_to_bcd_converter_8_p4
  Hex_Digit_Display R7d1 (.value(binary_to_bcd_converter_1_p3));  // open: dp
  Hex_Digit_Display R7d0 (.value(binary_to_bcd_converter_1_p4));  // open: dp
  Hex_Digit_Display R6d1 (.value(binary_to_bcd_converter_2_p3));  // open: dp
  Hex_Digit_Display R6d0 (.value(binary_to_bcd_converter_2_p4));  // open: dp
  Hex_Digit_Display R5d1 (.value(binary_to_bcd_converter_3_p3));  // open: dp
  Hex_Digit_Display R5d0 (.value(binary_to_bcd_converter_3_p4));  // open: dp
  Hex_Digit_Display R4d1 (.value(binary_to_bcd_converter_4_p3));  // open: dp
  Hex_Digit_Display R4d0 (.value(binary_to_bcd_converter_4_p4));  // open: dp
  Hex_Digit_Display R3dec1 (.value(binary_to_bcd_converter_5_p3));  // open: dp
  Hex_Digit_Display R3dec0 (.value(binary_to_bcd_converter_5_p4));  // open: dp
  Hex_Digit_Display R2dec1 (.value(binary_to_bcd_converter_6_p3));  // open: dp
  Hex_Digit_Display R2dec0 (.value(binary_to_bcd_converter_6_p4));  // open: dp
  Hex_Digit_Display R1dec1 (.value(binary_to_bcd_converter_7_p3));  // open: dp
  Hex_Digit_Display R1dec0 (.value(binary_to_bcd_converter_7_p4));  // open: dp
  Hex_Digit_Display R0dec1 (.value(binary_to_bcd_converter_8_p3));  // open: dp
  Hex_Digit_Display R0dec0 (.value(binary_to_bcd_converter_8_p4));  // open: dp
  Multiplexer #(.select(3), .width(8)) multiplexer_1 (
    .in0(R0o), .in1(R1o), .in2(R2o), .in3(R3o), .in4(R4o), .in5(R5o), .in6(R6o), .in7(R7o), .out(ope_A),
    .sel(dir_A));
  Multiplexer #(.select(2), .width(8)) multiplexer_2 (
    .in0(R0o), .in1(R1o), .in2(R2o), .in3(R3o), .out(ope_B), .sel(dir_B));
endmodule

module Preg_2 (
);

  wire clock_1_out, reset;
  wire [1:0] dir_b;
  wire [2:0] dir_A, operation;
  wire [7:0] adder_1_out, and_1_out, multiplexer_1_out, multiplexer_2_out, multiplexer_3_out, not_1_out,
       or_1_out, register_bank_8_1_ope_a, register_bank_8_1_ope_b, register_bank_8_1_r0o,
       register_bank_8_1_r1o, register_bank_8_1_r2o, register_bank_8_1_r3o, register_bank_8_1_r4o,
       register_bank_8_1_r5o, register_bank_8_1_r6o, register_bank_8_1_r7o, undriven;

  DotMatrix #(.matrixcols(8), .matrixrows(8)) dotmatrix_1 (
    .col0(register_bank_8_1_r7o), .col1(register_bank_8_1_r6o), .col2(register_bank_8_1_r5o),
    .col3(register_bank_8_1_r4o), .col4(register_bank_8_1_r3o), .col5(register_bank_8_1_r2o),
    .col6(register_bank_8_1_r1o), .col7(register_bank_8_1_r0o));
  Clock clock_1 (.out(clock_1_out));
  register_bank_8 register_bank_8_1 (
    .clock_reg(clock_1_out), .reset_reg(reset), .dir_DATO(dir_A), .dato(multiplexer_1_out), .dir_A(dir_A),
    .dir_B(dir_b), .ope_A(register_bank_8_1_ope_a), .R7o(register_bank_8_1_r7o), .R6o(register_bank_8_1_r6o),
    .R5o(register_bank_8_1_r5o), .R4o(register_bank_8_1_r4o), .R3o(register_bank_8_1_r3o),
    .R2o(register_bank_8_1_r2o), .R1o(register_bank_8_1_r1o), .R0o(register_bank_8_1_r0o),
    .ope_B(register_bank_8_1_ope_b));  // open: enable
  Multiplexer #(.select(3), .width(8)) multiplexer_1 (
    .in0(and_1_out), .in1(or_1_out), .in2(adder_1_out), .in3(register_bank_8_1_ope_b),
    .in4(multiplexer_2_out), .in5(multiplexer_3_out), .out(multiplexer_1_out), .sel(operation));  // open: in6, in7
  assign and_1_out = register_bank_8_1_ope_a & register_bank_8_1_ope_b;  // AND_Gate and_1, 8 bits wide
  assign or_1_out = register_bank_8_1_ope_a | register_bank_8_1_ope_b;  // OR_Gate or_1, 8 bits wide
  ROM rom_1 (.addr(undriven), .data({operation, dir_A, dir_b}));
  Adder adder_1 (.a(register_bank_8_1_ope_b), .b(register_bank_8_1_ope_a), .out(adder_1_out));  // open: cin, cout
  Button button_1 (.out(reset));
  Multiplexer #(.select(2), .width(8)) multiplexer_2 (
    .in0({register_bank_8_1_ope_a[6:0], 1'b0}), .in1({1'b0, register_bank_8_1_ope_a[7:1]}),
    .in2({register_bank_8_1_ope_a[6:0], register_bank_8_1_ope_a[7]}),
    .in3({register_bank_8_1_ope_a[0], register_bank_8_1_ope_a[7:1]}), .out(multiplexer_2_out), .sel(dir_b));
  assign not_1_out = ~register_bank_8_1_ope_a;  // NOT_Gate not_1, 8 bits wide
  Multiplexer #(.select(2), .width(8)) multiplexer_3 (
    .in0(not_1_out), .in1({8{1'b0}}), .in2({8{1'b1}}),
    .in3({register_bank_8_1_ope_a[3:0], register_bank_8_1_ope_a[7:4]}), .out(multiplexer_3_out), .sel(dir_b));

  // Other names for the same wires on the sheet: step_5[4:0] = {dir_A, dir_b}
endmodule
