// Logisim project clase_compu.circ as structural Verilog: 25 circuits, main circuit main
module main (
  input  [1:0] in_1,
  input  in_2,
  input  [1:0] in_3,
  input  [1:0] in_4,
  input  [1:0] in_5,
  input  [3:0] in_6,
  input  write_enable,
  input  [7:0] in_8,
  input  [7:0] instruction,
  input  in_10,
  input  [1:0] address,
  input  [7:0] dato,
  output out_13,
  output out_14,
  output [3:0] out_15
);

  wire button_1_out, button_2_out, button_3_out, button_4_out, button_5_out, button_6_out, button_7_out,
       clock_1_out, clock_2_out, clock_3_out, clock_4_out, decoder_1_out0, decoder_1_out1, decoder_2_out0,
       decoder_2_out1, decoder_2_out2, decoder_2_out3;
  wire [7:0] adder_1_out, adder_2_out, and_1_out, and_2_out, multiplexer_1_out, multiplexer_2_out, not_1_out,
       not_2_out, or_1_out, or_2_out, R0_q, R1_q, R2_q, R3_q, register_2_q, register_3_q,
       register_bank_4_1_ope_a, register_bank_4_1_ope_b, register_bank_4_2_ope_a, register_bank_4_2_ope_b;

  Button button_1 (.out(button_1_out));
  D_Flip_Flop d_ff_1 (
    .D(in_2), .clk(button_2_out), .Q(out_13), .Qn(out_14), .preset(button_1_out), .reset(button_3_out));
  Button button_2 (.out(button_2_out));
  Button button_3 (.out(button_3_out));
  Button button_4 (.out(button_4_out));
  Decoder decoder_1 (.out0(decoder_1_out0), .out1(decoder_1_out1), .sel(in_10));  // open: en
  Register #(.width(4)) register_1 (.D(in_6), .en(write_enable), .clk(button_4_out), .Q(out_15), .clr(button_5_out));
  Button button_5 (.out(button_5_out));
  Register register_2 (.D(in_8), .en(decoder_1_out0), .clk(clock_1_out), .Q(register_2_q));  // open: clr
  Register register_3 (.D(in_8), .en(decoder_1_out1), .clk(clock_1_out), .Q(register_3_q));  // open: clr
  Clock clock_1 (.out(clock_1_out));
  Decoder #(.select(2)) decoder_2 (
    .out0(decoder_2_out0), .out1(decoder_2_out1), .out2(decoder_2_out2), .out3(decoder_2_out3), .sel(address));  // open: en
  Register R0 (.D(dato), .en(decoder_2_out0), .clk(clock_2_out), .Q(R0_q));  // open: clr
  Register R1 (.D(dato), .en(decoder_2_out1), .clk(clock_2_out), .Q(R1_q));  // open: clr
  Register R2 (.D(dato), .en(decoder_2_out2), .clk(clock_2_out), .Q(R2_q));  // open: clr
  Register R3 (.D(dato), .en(decoder_2_out3), .clk(clock_2_out), .Q(R3_q));  // open: clr
  Clock clock_2 (.out(clock_2_out));
  Hex_Digit_Display hex_digit_display_1 (.value(register_2_q[7:4]));  // open: dp
  Hex_Digit_Display hex_digit_display_2 (.value(register_3_q[7:4]));  // open: dp
  Hex_Digit_Display hex_digit_display_3 (.value(register_2_q[3:0]));  // open: dp
  Hex_Digit_Display hex_digit_display_4 (.value(register_3_q[3:0]));  // open: dp
  Hex_Digit_Display hex_digit_display_5 (.value(R0_q[7:4]));  // open: dp
  Hex_Digit_Display hex_digit_display_6 (.value(R0_q[3:0]));  // open: dp
  Hex_Digit_Display hex_digit_display_7 (.value(R1_q[7:4]));  // open: dp
  Hex_Digit_Display hex_digit_display_8 (.value(R1_q[3:0]));  // open: dp
  Hex_Digit_Display hex_digit_display_9 (.value(R2_q[7:4]));  // open: dp
  Hex_Digit_Display hex_digit_display_10 (.value(R2_q[3:0]));  // open: dp
  Hex_Digit_Display hex_digit_display_11 (.value(R3_q[7:4]));  // open: dp
  Hex_Digit_Display hex_digit_display_12 (.value(R3_q[3:0]));  // open: dp
  ProgCounter_32 progcounter_32_1 ();  // open: reset_PC, clock_PC, PC
  Button button_6 (.out(button_6_out));
  Clock clock_3 (.out(clock_3_out));
  register_bank_4 register_bank_4_1 (
    .WRITE_address(in_4), .clock_reg(clock_3_out), .reset_reg(button_6_out), .dato(multiplexer_1_out),
    .dir_A(in_1), .dir_B(in_3), .ope_A(register_bank_4_1_ope_a), .ope_B(register_bank_4_1_ope_b));
  Button button_7 (.out(button_7_out));
  assign not_1_out = ~register_bank_4_1_ope_b;  // NOT_Gate not_1, 8 bits wide
  Multiplexer #(.select(2), .width(8)) multiplexer_1 (
    .in0(not_1_out), .in1(and_1_out), .in2(or_1_out), .in3(adder_1_out), .out(multiplexer_1_out), .sel(in_5));
  Clock clock_4 (.out(clock_4_out));
  assign and_1_out = register_bank_4_1_ope_b & register_bank_4_1_ope_a;  // AND_Gate and_1, 8 bits wide
  Multiplexer #(.select(2), .width(8)) multiplexer_2 (
    .in0(not_2_out), .in1(and_2_out), .in2(or_2_out), .in3(adder_2_out), .out(multiplexer_2_out),
    .sel(instruction[3:2]));
  register_bank_4 register_bank_4_2 (
    .WRITE_address(instruction[7:6]), .clock_reg(clock_4_out), .reset_reg(button_7_out),
    .dato(multiplexer_2_out), .dir_A(instruction[5:4]), .dir_B(instruction[1:0]),
    .ope_A(register_bank_4_2_ope_a), .ope_B(register_bank_4_2_ope_b));
  assign or_1_out = register_bank_4_1_ope_b | register_bank_4_1_ope_a;  // OR_Gate or_1, 8 bits wide
  assign not_2_out = ~register_bank_4_2_ope_b;  // NOT_Gate not_2, 8 bits wide
  assign and_2_out = register_bank_4_2_ope_b & register_bank_4_2_ope_a;  // AND_Gate and_2, 8 bits wide
  Adder adder_1 (.a(register_bank_4_1_ope_a), .b(register_bank_4_1_ope_b), .out(adder_1_out));  // open: cin, cout
  assign or_2_out = register_bank_4_2_ope_b | register_bank_4_2_ope_a;  // OR_Gate or_2, 8 bits wide
  Adder adder_2 (.a(register_bank_4_2_ope_a), .b(register_bank_4_2_ope_b), .out(adder_2_out));  // open: cin, cout

  // Other names for the same wires on the sheet: dir_b[1:0] = instruction[1:0]; operation[1:0] = instruction[3:2];
  //   dir_A[1:0] = instruction[5:4]; dir_RES[1:0] = instruction[7:6]
endmodule

module register_bank_4 (
  input  [1:0] dir_A,
  input  [1:0] dir_B,
  input  [1:0] WRITE_address,
  input  [7:0] dato,
  input  clock_reg,
  input  reset_reg,
  output [7:0] ope_A,
  output [7:0] ope_B
);

  wire decoder_1_out0, decoder_1_out1, decoder_1_out2, decoder_1_out3;
  wire [3:0] binary_to_bcd_converter_1_p2, binary_to_bcd_converter_1_p3, binary_to_bcd_converter_1_p4,
       binary_to_bcd_converter_2_p2, binary_to_bcd_converter_2_p3, binary_to_bcd_converter_2_p4,
       binary_to_bcd_converter_3_p2, binary_to_bcd_converter_3_p3, binary_to_bcd_converter_3_p4,
       binary_to_bcd_converter_4_p2, binary_to_bcd_converter_4_p3, binary_to_bcd_converter_4_p4, R0_q,
       R0_q_2, R1_q, R1_q_2, R2_q, R2_q_2, R3_q, R3_q_2;

  Decoder #(.select(2)) decoder_1 (
    .out0(decoder_1_out0), .out1(decoder_1_out1), .out2(decoder_1_out2), .out3(decoder_1_out3),
    .sel(WRITE_address));  // open: en
  Register R3 (.D(dato), .en(decoder_1_out3), .clk(clock_reg), .Q({R3_q_2, R3_q}), .clr(reset_reg));
  Register R2 (.D(dato), .en(decoder_1_out2), .clk(clock_reg), .Q({R2_q_2, R2_q}), .clr(reset_reg));
  Register R1 (.D(dato), .en(decoder_1_out1), .clk(clock_reg), .Q({R1_q_2, R1_q}), .clr(reset_reg));
  Register R0 (.D(dato), .en(decoder_1_out0), .clk(clock_reg), .Q({R0_q_2, R0_q}), .clr(reset_reg));
  Hex_Digit_Display R3_hex_H (.value(R3_q_2));  // open: dp
  Hex_Digit_Display R2_hex_H (.value(R2_q_2));  // open: dp
  Hex_Digit_Display R1_hex_H (.value(R1_q_2));  // open: dp
  Hex_Digit_Display R0_hex_H (.value(R0_q_2));  // open: dp
  Hex_Digit_Display R3_hex_L (.value(R3_q));  // open: dp
  Hex_Digit_Display R2_hex_L (.value(R2_q));  // open: dp
  Hex_Digit_Display R1_hex_L (.value(R1_q));  // open: dp
  Hex_Digit_Display R0_hex_L (.value(R0_q));  // open: dp
  Hex_Digit_Display R3dec2 (.value(binary_to_bcd_converter_1_p2));  // open: dp
  // Binary_to_BCD_converter #(.binvalue(8)) binary_to_bcd_converter_1: pin names not known; wires that end beside it: {R3_q_2, R3_q}, binary_to_bcd_converter_1_p2, binary_to_bcd_converter_1_p3, binary_to_bcd_converter_1_p4
  Hex_Digit_Display R2dec2 (.value(binary_to_bcd_converter_2_p2));  // open: dp
  // Binary_to_BCD_converter #(.binvalue(8)) binary_to_bcd_converter_2: pin names not known; wires that end beside it: {R2_q_2, R2_q}, binary_to_bcd_converter_2_p2, binary_to_bcd_converter_2_p3, binary_to_bcd_converter_2_p4
  Hex_Digit_Display R1dec2 (.value(binary_to_bcd_converter_3_p2));  // open: dp
  // Binary_to_BCD_converter #(.binvalue(8)) binary_to_bcd_converter_3: pin names not known; wires that end beside it: {R1_q_2, R1_q}, binary_to_bcd_converter_3_p2, binary_to_bcd_converter_3_p3, binary_to_bcd_converter_3_p4
  Hex_Digit_Display R0dec2 (.value(binary_to_bcd_converter_4_p2));  // open: dp
  // Binary_to_BCD_converter #(.binvalue(8)) binary_to_bcd_converter_4: pin names not known; wires that end beside it: {R0_q_2, R0_q}, binary_to_bcd_converter_4_p2, binary_to_bcd_converter_4_p3, binary_to_bcd_converter_4_p4
  Hex_Digit_Display R3dec1 (.value(binary_to_bcd_converter_1_p3));  // open: dp
  Hex_Digit_Display R3dec0 (.value(binary_to_bcd_converter_1_p4));  // open: dp
  Hex_Digit_Display R2dec1 (.value(binary_to_bcd_converter_2_p3));  // open: dp
  Hex_Digit_Display R2dec0 (.value(binary_to_bcd_converter_2_p4));  // open: dp
  Hex_Digit_Display R1dec1 (.value(binary_to_bcd_converter_3_p3));  // open: dp
  Hex_Digit_Display R1dec0 (.value(binary_to_bcd_converter_3_p4));  // open: dp
  Hex_Digit_Display R0dec1 (.value(binary_to_bcd_converter_4_p3));  // open: dp
  Hex_Digit_Display R0dec0 (.value(binary_to_bcd_converter_4_p4));  // open: dp
  Multiplexer #(.select(2), .width(8)) multiplexer_1 (
    .in0({R0_q_2, R0_q}), .in1({R1_q_2, R1_q}), .in2({R2_q_2, R2_q}), .in3({R3_q_2, R3_q}), .out(ope_A),
    .sel(dir_A));
  Multiplexer #(.select(2), .width(8)) multiplexer_2 (
    .in0({R0_q_2, R0_q}), .in1({R1_q_2, R1_q}), .in2({R2_q_2, R2_q}), .in3({R3_q_2, R3_q}), .out(ope_B),
    .sel(dir_B));
endmodule

module preg1 (
);

  wire clock_1_out, clock_2_out, reset;
  wire [1:0] dir_A, dir_b, dir_RES, operation;
  wire [4:0] progcounter_32_1_pc;
  wire [7:0] adder_1_out, and_1_out, multiplexer_1_out, not_1_out, or_1_out, register_bank_4_1_ope_a,
       register_bank_4_1_ope_b;

  ProgCounter_32 progcounter_32_1 (.reset_PC(reset), .clock_PC(clock_1_out), .PC(progcounter_32_1_pc));
  ROM #(.addrWidth(5)) rom_1 (.addr(progcounter_32_1_pc), .data({dir_RES, dir_A, operation, dir_b}));
  Clock clock_1 (.out(clock_1_out));
  Button button_1 (.out(reset));
  Clock clock_2 (.out(clock_2_out));
  Multiplexer #(.select(2), .width(8)) multiplexer_1 (
    .in0(not_1_out), .in1(and_1_out), .in2(or_1_out), .in3(adder_1_out), .out(multiplexer_1_out),
    .sel(operation));
  register_bank_4 register_bank_4_1 (
    .WRITE_address(dir_RES), .clock_reg(clock_2_out), .reset_reg(reset), .dato(multiplexer_1_out),
    .dir_A(dir_A), .dir_B(dir_b), .ope_A(register_bank_4_1_ope_a), .ope_B(register_bank_4_1_ope_b));
  assign not_1_out = ~register_bank_4_1_ope_b;  // NOT_Gate not_1, 8 bits wide
  assign and_1_out = register_bank_4_1_ope_b & register_bank_4_1_ope_a;  // AND_Gate and_1, 8 bits wide
  assign or_1_out = register_bank_4_1_ope_b | register_bank_4_1_ope_a;  // OR_Gate or_1, 8 bits wide
  Adder adder_1 (.a(register_bank_4_1_ope_a), .b(register_bank_4_1_ope_b), .out(adder_1_out));  // open: cin, cout

  // Notes on the sheet:
  //   contents of rom_1 (hex, n*v repeats v):
  //   0 41 8d 82 8*e 6*5e ef ef af
endmodule

module ProgCounter_16 (
  input  reset_PC,
  input  clock_PC,
  output [3:0] PC
);

  Counter #(.max('hf), .width(4)) counter_1 (
    .clr(reset_PC), .load(1'b0), .up(1'b1), .count(1'b1), .clk(clock_PC), .Q(PC));  // open: D, carry
  Hex_Digit_Display hex_digit_display_1 (.value(PC));  // open: dp
endmodule

module ProgCounter_32 (
  input  reset_PC,
  input  clock_PC,
  output [4:0] PC
);

  wire [3:0] binary_to_bcd_converter_1_p2, binary_to_bcd_converter_1_p3;

  Counter #(.max('h1f), .width(5)) counter_1 (
    .clr(reset_PC), .load(1'b0), .up(1'b1), .count(1'b1), .clk(clock_PC), .Q(PC));  // open: D, carry
  Hex_Digit_Display hex1 (.value({3'b000, PC[4]}));  // open: dp
  Hex_Digit_Display hex0 (.value(PC[3:0]));  // open: dp
  Hex_Digit_Display dec1 (.value(binary_to_bcd_converter_1_p2));  // open: dp
  // Binary_to_BCD_converter #(.binvalue(5)) binary_to_bcd_converter_1: pin names not known; wires that end beside it: PC, binary_to_bcd_converter_1_p2, binary_to_bcd_converter_1_p3
  Hex_Digit_Display dec0 (.value(binary_to_bcd_converter_1_p3));  // open: dp
endmodule

module preg2 (
);

  wire clock_1_out, clock_2_out, reset;
  wire [1:0] dir_b;
  wire [2:0] dir_A, operation;
  wire [4:0] progcounter_32_1_pc;
  wire [7:0] adder_1_out, and_1_out, multiplexer_1_out, not_1_out, or_1_out, register_bank_8_1_ope_a,
       register_bank_8_1_ope_b;

  ProgCounter_32 progcounter_32_1 (.reset_PC(reset), .clock_PC(clock_2_out), .PC(progcounter_32_1_pc));
  ROM #(.addrWidth(5)) asd (.addr(progcounter_32_1_pc), .data({operation, dir_A, dir_b}));
  Clock clock_1 (.out(clock_1_out));
  Clock clock_2 (.out(clock_2_out));
  register_bank_8 register_bank_8_1 (
    .clock_reg(clock_1_out), .reset_reg(reset), .dir_DATO(dir_A), .dato(multiplexer_1_out), .dir_A(dir_A),
    .dir_B(dir_b), .ope_A(register_bank_8_1_ope_a), .ope_B(register_bank_8_1_ope_b));  // open: enable, R7
  Multiplexer #(.select(3), .width(8)) multiplexer_1 (
    .in0(and_1_out), .in1(or_1_out), .in2(adder_1_out), .in3(register_bank_8_1_ope_b), .in4(not_1_out),
    .in5({register_bank_8_1_ope_a[6:0], 1'b0}), .in6({1'b0, register_bank_8_1_ope_a[7:1]}),
    .in7({{6{1'b0}}, dir_b}), .out(multiplexer_1_out), .sel(operation));
  assign and_1_out = register_bank_8_1_ope_a & register_bank_8_1_ope_b;  // AND_Gate and_1, 8 bits wide
  assign or_1_out = register_bank_8_1_ope_a | register_bank_8_1_ope_b;  // OR_Gate or_1, 8 bits wide
  Adder adder_1 (.a(register_bank_8_1_ope_b), .b(register_bank_8_1_ope_a), .out(adder_1_out));  // open: cin, cout
  assign not_1_out = ~register_bank_8_1_ope_a;  // NOT_Gate not_1, 8 bits wide
  Button button_1 (.out(reset));

  // Notes on the sheet:
  //   bits dir_B actúan como
  //   un inmediato de 2 bits
endmodule

module register_bank_8 (
  input  [2:0] dir_DATO,
  input  enable,
  input  [2:0] dir_A,
  input  [1:0] dir_B,
  input  [7:0] dato,
  input  clock_reg,
  input  reset_reg,
  output [7:0] ope_A,
  output [7:0] ope_B,
  output [7:0] R7
);

  wire decoder_1_out0, decoder_1_out1, decoder_1_out2, decoder_1_out3, decoder_1_out4, decoder_1_out5,
       decoder_1_out6, decoder_1_out7;
  wire [3:0] binary_to_bcd_converter_1_p2, binary_to_bcd_converter_1_p3, binary_to_bcd_converter_1_p4,
       binary_to_bcd_converter_2_p2, binary_to_bcd_converter_2_p3, binary_to_bcd_converter_2_p4,
       binary_to_bcd_converter_3_p2, binary_to_bcd_converter_3_p3, binary_to_bcd_converter_3_p4,
       binary_to_bcd_converter_4_p2, binary_to_bcd_converter_4_p3, binary_to_bcd_converter_4_p4,
       binary_to_bcd_converter_5_p2, binary_to_bcd_converter_5_p3, binary_to_bcd_converter_5_p4,
       binary_to_bcd_converter_6_p2, binary_to_bcd_converter_6_p3, binary_to_bcd_converter_6_p4,
       binary_to_bcd_converter_7_p2, binary_to_bcd_converter_7_p3, binary_to_bcd_converter_7_p4,
       binary_to_bcd_converter_8_p2, binary_to_bcd_converter_8_p3, binary_to_bcd_converter_8_p4, R0_q,
       R0_q_2, R1_q, R1_q_2, R2_q, R2_q_2, R3_q, R3_q_2, register_2_q, register_2_q_2, register_3_q,
       register_3_q_2, register_4_q, register_4_q_2;

  Decoder #(.select(3)) decoder_1 (
    .out0(decoder_1_out0), .out1(decoder_1_out1), .out2(decoder_1_out2), .out3(decoder_1_out3),
    .out4(decoder_1_out4), .out5(decoder_1_out5), .out6(decoder_1_out6), .out7(decoder_1_out7),
    .sel(dir_DATO), .en(enable));
  Register register_1 (.D(dato), .en(decoder_1_out7), .clk(clock_reg), .Q(R7), .clr(reset_reg));
  Register register_2 (
    .D(dato), .en(decoder_1_out6), .clk(clock_reg), .Q({register_2_q_2, register_2_q}), .clr(reset_reg));
  Register register_3 (
    .D(dato), .en(decoder_1_out5), .clk(clock_reg), .Q({register_3_q_2, register_3_q}), .clr(reset_reg));
  Register register_4 (
    .D(dato), .en(decoder_1_out4), .clk(clock_reg), .Q({register_4_q_2, register_4_q}), .clr(reset_reg));
  Register R3 (.D(dato), .en(decoder_1_out3), .clk(clock_reg), .Q({R3_q_2, R3_q}), .clr(reset_reg));
  Register R2 (.D(dato), .en(decoder_1_out2), .clk(clock_reg), .Q({R2_q_2, R2_q}), .clr(reset_reg));
  Register R1 (.D(dato), .en(decoder_1_out1), .clk(clock_reg), .Q({R1_q_2, R1_q}), .clr(reset_reg));
  Register R0 (.D(dato), .en(decoder_1_out0), .clk(clock_reg), .Q({R0_q_2, R0_q}), .clr(reset_reg));
  Hex_Digit_Display R7_h_H (.value(R7[7:4]));  // open: dp
  Hex_Digit_Display R6_h_H (.value(register_2_q_2));  // open: dp
  Hex_Digit_Display R5_h_H (.value(register_3_q_2));  // open: dp
  Hex_Digit_Display R4_h_H (.value(register_4_q_2));  // open: dp
  Hex_Digit_Display R3_hex_H (.value(R3_q_2));  // open: dp
  Hex_Digit_Display R2_hex_H (.value(R2_q_2));  // open: dp
  Hex_Digit_Display R1_hex_H (.value(R1_q_2));  // open: dp
  Hex_Digit_Display R0_hex_H (.value(R0_q_2));  // open: dp
  Hex_Digit_Display R7_h_L (.value(R7[3:0]));  // open: dp
  Hex_Digit_Display R6_h_L (.value(register_2_q));  // open: dp
  Hex_Digit_Display R5_h_L (.value(register_3_q));  // open: dp
  Hex_Digit_Display R4_h_L (.value(register_4_q));  // open: dp
  Hex_Digit_Display R3_hex_L (.value(R3_q));  // open: dp
  Hex_Digit_Display R2_hex_L (.value(R2_q));  // open: dp
  Hex_Digit_Display R1_hex_L (.value(R1_q));  // open: dp
  Hex_Digit_Display R0_hex_L (.value(R0_q));  // open: dp
  Hex_Digit_Display R7d2 (.value(binary_to_bcd_converter_1_p2));  // open: dp
  // Binary_to_BCD_converter #(.binvalue(8)) binary_to_bcd_converter_1: pin names not known; wires that end beside it: R7, binary_to_bcd_converter_1_p2, binary_to_bcd_converter_1_p3, binary_to_bcd_converter_1_p4
  Hex_Digit_Display R6d2 (.value(binary_to_bcd_converter_2_p2));  // open: dp
  // Binary_to_BCD_converter #(.binvalue(8)) binary_to_bcd_converter_2: pin names not known; wires that end beside it: {register_2_q_2, register_2_q}, binary_to_bcd_converter_2_p2, binary_to_bcd_converter_2_p3, binary_to_bcd_converter_2_p4
  Hex_Digit_Display R5d2 (.value(binary_to_bcd_converter_3_p2));  // open: dp
  // Binary_to_BCD_converter #(.binvalue(8)) binary_to_bcd_converter_3: pin names not known; wires that end beside it: {register_3_q_2, register_3_q}, binary_to_bcd_converter_3_p2, binary_to_bcd_converter_3_p3, binary_to_bcd_converter_3_p4
  Hex_Digit_Display R4d2 (.value(binary_to_bcd_converter_4_p2));  // open: dp
  // Binary_to_BCD_converter #(.binvalue(8)) binary_to_bcd_converter_4: pin names not known; wires that end beside it: {register_4_q_2, register_4_q}, binary_to_bcd_converter_4_p2, binary_to_bcd_converter_4_p3, binary_to_bcd_converter_4_p4
  Hex_Digit_Display R3dec2 (.value(binary_to_bcd_converter_5_p2));  // open: dp
  // Binary_to_BCD_converter #(.binvalue(8)) binary_to_bcd_converter_5: pin names not known; wires that end beside it: {R3_q_2, R3_q}, binary_to_bcd_converter_5_p2, binary_to_bcd_converter_5_p3, binary_to_bcd_converter_5_p4
  Hex_Digit_Display R2dec2 (.value(binary_to_bcd_converter_6_p2));  // open: dp
  // Binary_to_BCD_converter #(.binvalue(8)) binary_to_bcd_converter_6: pin names not known; wires that end beside it: {R2_q_2, R2_q}, binary_to_bcd_converter_6_p2, binary_to_bcd_converter_6_p3, binary_to_bcd_converter_6_p4
  Hex_Digit_Display R1dec2 (.value(binary_to_bcd_converter_7_p2));  // open: dp
  // Binary_to_BCD_converter #(.binvalue(8)) binary_to_bcd_converter_7: pin names not known; wires that end beside it: {R1_q_2, R1_q}, binary_to_bcd_converter_7_p2, binary_to_bcd_converter_7_p3, binary_to_bcd_converter_7_p4
  Hex_Digit_Display R0dec2 (.value(binary_to_bcd_converter_8_p2));  // open: dp
  // Binary_to_BCD_converter #(.binvalue(8)) binary_to_bcd_converter_8: pin names not known; wires that end beside it: {R0_q_2, R0_q}, binary_to_bcd_converter_8_p2, binary_to_bcd_converter_8_p3, binary_to_bcd_converter_8_p4
  Hex_Digit_Display R7d1 (.value(binary_to_bcd_converter_1_p3));  // open: dp
  Hex_Digit_Display R7d0 (.value(binary_to_bcd_converter_1_p4));  // open: dp
  Hex_Digit_Display R6d1 (.value(binary_to_bcd_converter_2_p3));  // open: dp
  Hex_Digit_Display R6d0 (.value(binary_to_bcd_converter_2_p4));  // open: dp
  Hex_Digit_Display R5d1 (.value(binary_to_bcd_converter_3_p3));  // open: dp
  Hex_Digit_Display R5d0 (.value(binary_to_bcd_converter_3_p4));  // open: dp
  Hex_Digit_Display R4d1 (.value(binary_to_bcd_converter_4_p3));  // open: dp
  Hex_Digit_Display R4d0 (.value(binary_to_bcd_converter_4_p4));  // open: dp
  Hex_Digit_Display R3dec1 (.value(binary_to_bcd_converter_5_p3));  // open: dp
  Hex_Digit_Display R3dec0 (.value(binary_to_bcd_converter_5_p4));  // open: dp
  Hex_Digit_Display R2dec1 (.value(binary_to_bcd_converter_6_p3));  // open: dp
  Hex_Digit_Display R2dec0 (.value(binary_to_bcd_converter_6_p4));  // open: dp
  Hex_Digit_Display R1dec1 (.value(binary_to_bcd_converter_7_p3));  // open: dp
  Hex_Digit_Display R1dec0 (.value(binary_to_bcd_converter_7_p4));  // open: dp
  Hex_Digit_Display R0dec1 (.value(binary_to_bcd_converter_8_p3));  // open: dp
  Hex_Digit_Display R0dec0 (.value(binary_to_bcd_converter_8_p4));  // open: dp
  Multiplexer #(.select(3), .width(8)) multiplexer_1 (
    .in0({R0_q_2, R0_q}), .in1({R1_q_2, R1_q}), .in2({R2_q_2, R2_q}), .in3({R3_q_2, R3_q}),
    .in4({register_4_q_2, register_4_q}), .in5({register_3_q_2, register_3_q}),
    .in6({register_2_q_2, register_2_q}), .in7(R7), .out(ope_A), .sel(dir_A));
  Multiplexer #(.select(2), .width(8)) multiplexer_2 (
    .in0({R0_q_2, R0_q}), .in1({R1_q_2, R1_q}), .in2({R2_q_2, R2_q}), .in3({R3_q_2, R3_q}), .out(ope_B),
    .sel(dir_B));
endmodule

module compu_3 (
);

  wire clock_1_out, clock_2_out, no_reg, not_1_out, reset;
  wire [1:0] dir_b;
  wire [2:0] dir_A, operation, xnor_1_out;
  wire [7:0] adder_1_out, and_2_out, multiplexer_1_out, multiplexer_2_out, multiplexer_3_out, not_2_out,
       or_1_out, progcounter_guapo_1_1_pc, register_bank_8_1_ope_a, register_bank_8_1_ope_b;

  and and_1 (no_reg, xnor_1_out[2], xnor_1_out[1], xnor_1_out[0]);
  ProgCounter_guapo_1 progcounter_guapo_1_1 (
    .step({dir_A, dir_b}), .reset(reset), .load_count(no_reg), .clock(clock_1_out),
    .PC(progcounter_guapo_1_1_pc));
  Clock clock_1 (.out(clock_1_out));
  assign xnor_1_out = ~(operation ^ 3'b110);  // XNOR_Gate xnor_1, 3 bits wide
  not not_1 (not_1_out, no_reg);
  ROM rom_1 (.addr(progcounter_guapo_1_1_pc), .data({operation, dir_A, dir_b}));
  Clock clock_2 (.out(clock_2_out));
  register_bank_8 register_bank_8_1 (
    .clock_reg(clock_2_out), .reset_reg(reset), .enable(not_1_out), .dir_DATO(dir_A),
    .dato(multiplexer_1_out), .dir_A(dir_A), .dir_B(dir_b), .ope_A(register_bank_8_1_ope_a),
    .ope_B(register_bank_8_1_ope_b));  // open: R7
  Multiplexer #(.select(3), .width(8)) multiplexer_1 (
    .in0(and_2_out), .in1(or_1_out), .in2(adder_1_out), .in3(register_bank_8_1_ope_b),
    .in4(multiplexer_2_out), .in5(multiplexer_3_out), .out(multiplexer_1_out), .sel(operation));  // open: in6, in7
  assign and_2_out = register_bank_8_1_ope_a & register_bank_8_1_ope_b;  // AND_Gate and_2, 8 bits wide
  assign or_1_out = register_bank_8_1_ope_a | register_bank_8_1_ope_b;  // OR_Gate or_1, 8 bits wide
  Adder adder_1 (.a(register_bank_8_1_ope_b), .b(register_bank_8_1_ope_a), .out(adder_1_out));  // open: cin, cout
  Button button_1 (.out(reset));
  RAM ram_1 ();  // open: addr, we, oe, clk, din, dout
  Multiplexer #(.select(2), .width(8)) multiplexer_2 (
    .in0({register_bank_8_1_ope_a[6:0], 1'b0}), .in1({1'b0, register_bank_8_1_ope_a[7:1]}),
    .in2({register_bank_8_1_ope_a[6:0], register_bank_8_1_ope_a[7]}),
    .in3({register_bank_8_1_ope_a[0], register_bank_8_1_ope_a[7:1]}), .out(multiplexer_2_out), .sel(dir_b));
  assign not_2_out = ~register_bank_8_1_ope_a;  // NOT_Gate not_2, 8 bits wide
  Multiplexer #(.select(2), .width(8)) multiplexer_3 (
    .in0(not_2_out), .in1({8{1'b0}}), .in2({8{1'b1}}),
    .in3({register_bank_8_1_ope_a[3:0], register_bank_8_1_ope_a[7:4]}), .out(multiplexer_3_out), .sel(dir_b));
  DotMatrix dotmatrix_1 ();  // open: col0, col1, col2, col3, col4

  // Other names for the same wires on the sheet: step_5[4:0] = {dir_A, dir_b}

  // Notes on the sheet:
  //   contents of rom_1 (hex, n*v repeats v):
  //   a0 a6 81 81 84 84 84 a3 a0 a4 49 6c 2e b0 13 b3 8f 92 a1 c2 c0 bc bc
  //   bits dir_B actúan como
  //   un inmediato de 2 bits
endmodule

module ProgCounter_guapo_1 (
  input  reset,
  input  load_count,
  input  clock,
  input  [4:0] step,
  output [7:0] PC
);

  wire [3:0] binary_to_bcd_converter_1_p2, binary_to_bcd_converter_1_p3, binary_to_bcd_converter_1_p4;
  wire [7:0] adder_1_out;

  Counter counter_1 (.clr(reset), .load(load_count), .clk(clock), .D(adder_1_out), .Q(PC));  // open: up, count, carry
  Adder adder_1 (.a(PC), .b({3'b000, step}), .out(adder_1_out));  // open: cin, cout
  Hex_Digit_Display dec2 (.value(binary_to_bcd_converter_1_p2));  // open: dp
  Hex_Digit_Display dec1 (.value(binary_to_bcd_converter_1_p3));  // open: dp
  // Binary_to_BCD_converter #(.binvalue(8)) binary_to_bcd_converter_1: pin names not known; wires that end beside it: PC, binary_to_bcd_converter_1_p2, binary_to_bcd_converter_1_p3, binary_to_bcd_converter_1_p4
  Hex_Digit_Display hex1 (.value(PC[7:4]));  // open: dp
  Hex_Digit_Display dec0 (.value(binary_to_bcd_converter_1_p4));  // open: dp
  Hex_Digit_Display hex0 (.value(PC[3:0]));  // open: dp
endmodule

module compu_4 (
);

  wire clock_1_out, clock_2_out, no_reg, not_1_out, reset;
  wire [1:0] dir_b;
  wire [2:0] dir_A, operation, xnor_1_out;
  wire [7:0] adder_1_out, and_2_out, counter_8_1_pc, multiplexer_1_out, multiplexer_2_out, multiplexer_3_out,
       multiplexer_4_out, not_2_out, or_1_out, register_bank_8_1_ope_a, register_bank_8_1_ope_b;

  assign xnor_1_out = ~(operation ^ 3'b110);  // XNOR_Gate xnor_1, 3 bits wide
  and and_1 (no_reg, xnor_1_out[2], xnor_1_out[1], xnor_1_out[0]);
  Multiplexer #(.width(8)) multiplexer_1 (
    .in0(8'h1), .in1({3'b000, dir_A, dir_b}), .out(multiplexer_1_out), .sel(no_reg));
  Clock clock_1 (.out(clock_1_out));
  Counter_8 counter_8_1 (.EN(1'b1), .step(multiplexer_1_out), .clk(clock_1_out), .reset(reset), .PC(counter_8_1_pc));
  not not_1 (not_1_out, no_reg);
  ROM rom_1 (.addr(counter_8_1_pc), .data({operation, dir_A, dir_b}));
  Clock clock_2 (.out(clock_2_out));
  register_bank_8 register_bank_8_1 (
    .clock_reg(clock_2_out), .reset_reg(reset), .enable(not_1_out), .dir_DATO(dir_A),
    .dato(multiplexer_2_out), .dir_A(dir_A), .dir_B(dir_b), .ope_A(register_bank_8_1_ope_a),
    .ope_B(register_bank_8_1_ope_b));  // open: R7
  Multiplexer #(.select(3), .width(8)) multiplexer_2 (
    .in0(and_2_out), .in1(or_1_out), .in2(adder_1_out), .in3(register_bank_8_1_ope_b),
    .in4(multiplexer_3_out), .in5(multiplexer_4_out), .out(multiplexer_2_out), .sel(operation));  // open: in6, in7
  assign and_2_out = register_bank_8_1_ope_a & register_bank_8_1_ope_b;  // AND_Gate and_2, 8 bits wide
  assign or_1_out = register_bank_8_1_ope_a | register_bank_8_1_ope_b;  // OR_Gate or_1, 8 bits wide
  Adder adder_1 (.a(register_bank_8_1_ope_b), .b(register_bank_8_1_ope_a), .out(adder_1_out));  // open: cin, cout
  Button button_1 (.out(reset));
  Multiplexer #(.select(2), .width(8)) multiplexer_3 (
    .in0({register_bank_8_1_ope_a[6:0], 1'b0}), .in1({1'b0, register_bank_8_1_ope_a[7:1]}),
    .in2({register_bank_8_1_ope_a[6:0], register_bank_8_1_ope_a[7]}),
    .in3({register_bank_8_1_ope_a[0], register_bank_8_1_ope_a[7:1]}), .out(multiplexer_3_out), .sel(dir_b));
  assign not_2_out = ~register_bank_8_1_ope_a;  // NOT_Gate not_2, 8 bits wide
  Multiplexer #(.select(2), .width(8)) multiplexer_4 (
    .in0(not_2_out), .in1({8{1'b0}}), .in2({8{1'b1}}),
    .in3({register_bank_8_1_ope_a[3:0], register_bank_8_1_ope_a[7:4]}), .out(multiplexer_4_out), .sel(dir_b));

  // Other names for the same wires on the sheet: step_5[4:0] = {dir_A, dir_b}

  // Notes on the sheet:
  //   contents of rom_1 (hex, n*v repeats v):
  //   a0 a6 81 81 84 84 84 a3 a0 a4 49 6c 2e b0 13 b3 8f 92 a1 c2 c0 bc bc c0
endmodule

module Counter_8 (
  input  [7:0] step,
  input  EN,
  input  clk,
  input  reset,
  output [7:0] PC
);

  wire [3:0] binary_to_bcd_converter_1_p2, binary_to_bcd_converter_1_p3, binary_to_bcd_converter_1_p4;
  wire [7:0] adder_1_out;

  Adder adder_1 (.a(PC), .b(step), .out(adder_1_out));  // open: cin, cout
  Register register_1 (.D(adder_1_out), .en(EN), .clk(clk), .Q(PC), .clr(reset));
  Hex_Digit_Display h1 (.value(PC[7:4]));  // open: dp
  Hex_Digit_Display h0 (.value(PC[3:0]));  // open: dp
  Hex_Digit_Display d2 (.value(binary_to_bcd_converter_1_p2));  // open: dp
  // Binary_to_BCD_converter #(.binvalue(8)) binary_to_bcd_converter_1: pin names not known; wires that end beside it: PC, binary_to_bcd_converter_1_p2, binary_to_bcd_converter_1_p3, binary_to_bcd_converter_1_p4
  Hex_Digit_Display d1 (.value(binary_to_bcd_converter_1_p3));  // open: dp
  Hex_Digit_Display d0 (.value(binary_to_bcd_converter_1_p4));  // open: dp
endmodule

module compu_5 (
  output [7:0] out_1,
  output [7:0] out_2
);

  wire clock_1_out, clock_2_out, clock_3_out, no_reg, nor_1_out, RAM_WRITE, reset;
  wire [1:0] dir_b;
  wire [2:0] dir_A, operation, xnor_1_out;
  wire [7:0] adder_1_out, and_2_out, counter_8_1_pc, multiplexer_1_out, multiplexer_2_out, multiplexer_3_out,
       multiplexer_4_out, not_1_out, opeA, or_1_out, register_bank_8_1_ope_b;

  assign xnor_1_out = ~(operation ^ 3'b110);  // XNOR_Gate xnor_1, 3 bits wide
  and and_1 (no_reg, xnor_1_out[2], xnor_1_out[1], xnor_1_out[0]);
  Multiplexer #(.width(8)) multiplexer_1 (
    .in0(8'h1), .in1({3'b000, dir_A, dir_b}), .out(multiplexer_1_out), .sel(no_reg));
  Clock clock_1 (.out(clock_1_out));
  ROM rom_1 (.addr(counter_8_1_pc), .data({operation, dir_A, dir_b}));
  Counter_8 counter_8_1 (.EN(1'b1), .step(multiplexer_1_out), .clk(clock_1_out), .reset(reset), .PC(counter_8_1_pc));
  nor nor_1 (nor_1_out, RAM_WRITE, no_reg);
  Clock clock_2 (.out(clock_2_out));
  register_bank_8 register_bank_8_1 (
    .clock_reg(clock_2_out), .reset_reg(reset), .enable(nor_1_out), .dir_DATO(dir_A),
    .dato(multiplexer_2_out), .dir_A(dir_A), .dir_B(dir_b), .ope_A(opeA), .R7(out_2),
    .ope_B(register_bank_8_1_ope_b));
  Multiplexer #(.select(3), .width(8)) multiplexer_2 (
    .in0(and_2_out), .in1(or_1_out), .in2(adder_1_out), .in3(register_bank_8_1_ope_b),
    .in4(multiplexer_3_out), .in5(multiplexer_4_out), .in7(out_1), .out(multiplexer_2_out), .sel(operation));  // open: in6
  assign and_2_out = opeA & register_bank_8_1_ope_b;  // AND_Gate and_2, 8 bits wide
  assign or_1_out = opeA | register_bank_8_1_ope_b;  // OR_Gate or_1, 8 bits wide
  Adder adder_1 (.a(register_bank_8_1_ope_b), .b(opeA), .out(adder_1_out));  // open: cin, cout
  Button button_1 (.out(reset));
  Multiplexer #(.select(2), .width(8)) multiplexer_3 (
    .in0({opeA[6:0], 1'b0}), .in1({1'b0, opeA[7:1]}), .in2({opeA[6:0], opeA[7]}), .in3({opeA[0], opeA[7:1]}),
    .out(multiplexer_3_out), .sel(dir_b));
  and and_3 (RAM_WRITE, dir_b[0], operation[0], operation[1], operation[2]);
  Clock clock_3 (.out(clock_3_out));
  assign not_1_out = ~opeA;  // NOT_Gate not_1, 8 bits wide
  Multiplexer #(.select(2), .width(8)) multiplexer_4 (
    .in0(not_1_out), .in1({8{1'b0}}), .in2({8{1'b1}}), .in3({opeA[3:0], opeA[7:4]}), .out(multiplexer_4_out),
    .sel(dir_b));
  RAM #(.asyncread("true")) ram_1 (
    .addr(out_2), .we(RAM_WRITE), .oe(1'b1), .clk(clock_3_out), .din(opeA), .dout(out_1));

  // Other names for the same wires on the sheet: R_W = dir_b[0]; step_5[4:0] = {dir_A, dir_b};
  //   pointer_R7[7:0] = out_2

  // Notes on the sheet:
  //   contents of rom_1 (hex, n*v repeats v):
  //   a0 a6 81 81 84 84 84 a3 a0 a4 49 6c 2e b0 13 b3 8f 92 a1 c2 c0 bc bc 7e f8 5e f1 c0
endmodule

module display_8bits (
  input  [7:0] in_1
);

  wire [3:0] binary_to_bcd_converter_1_p2, binary_to_bcd_converter_1_p3, binary_to_bcd_converter_1_p4;

  Hex_Digit_Display h1 (.value(in_1[7:4]));  // open: dp
  Hex_Digit_Display h0 (.value(in_1[3:0]));  // open: dp
  Hex_Digit_Display d2 (.value(binary_to_bcd_converter_1_p2));  // open: dp
  // Binary_to_BCD_converter #(.binvalue(8)) binary_to_bcd_converter_1: pin names not known; wires that end beside it: in_1, binary_to_bcd_converter_1_p2, binary_to_bcd_converter_1_p3, binary_to_bcd_converter_1_p4
  Hex_Digit_Display d1 (.value(binary_to_bcd_converter_1_p3));  // open: dp
  Hex_Digit_Display d0 (.value(binary_to_bcd_converter_1_p4));  // open: dp
endmodule

module display_3bits (
  input  [2:0] in_1
);

  Hex_Digit_Display h0 (.value({1'b0, in_1}));  // open: dp
endmodule

module display_2bits (
  input  [1:0] in_1
);

  Hex_Digit_Display h0 (.value({2'b00, in_1}));  // open: dp
endmodule

module comp_3bits (
  input  [2:0] N,
  input  [2:0] \ref ,
  output Y
);

  wire [2:0] xnor_1_out;

  assign xnor_1_out = ~(N ^ \ref );  // XNOR_Gate xnor_1, 3 bits wide
  and and_1 (Y, xnor_1_out[2], xnor_1_out[1], xnor_1_out[0]);
endmodule

module compu_6 (
);

  wire clock_1_out, clock_2_out, clock_3_out, comparator_1_eq, no_reg, nor_1_out, RAM_WRITE, reset;
  wire [1:0] dir_b;
  wire [2:0] dir_A, xnor_1_out;
  wire [7:0] adder_1_out, adder_2_out, and_2_out, multiplexer_1_out, multiplexer_2_out, multiplexer_3_out,
       multiplexer_4_out, multiplexer_5_out, not_1_out, opeA, or_1_out, pointer_R7, ram_1_dout, register_1_q,
       register_bank_8_1_ope_b;
  wire [7:5] instruction;

  assign xnor_1_out = ~(instruction ^ 3'b110);  // XNOR_Gate xnor_1, 3 bits wide
  and and_1 (no_reg, xnor_1_out[2], xnor_1_out[1], xnor_1_out[0]);
  Multiplexer #(.width(8)) multiplexer_1 (
    .in0(8'h1), .in1({3'b000, dir_A, dir_b}), .out(multiplexer_1_out), .sel(no_reg));
  Adder adder_1 (.a(register_1_q), .b(multiplexer_1_out), .out(adder_1_out));  // open: cin, cout
  Comparator comparator_1 (.a(8'hc1), .b({instruction, dir_A, dir_b}), .eq(comparator_1_eq));  // open: gt, lt
  display_8bits display_8bits_1 (.in_1(register_1_q));
  Register register_1 (.D(multiplexer_2_out), .clk(clock_1_out), .Q(register_1_q), .clr(reset));  // open: en
  Multiplexer #(.width(8)) multiplexer_2 (
    .in0(adder_1_out), .in1(pointer_R7), .out(multiplexer_2_out), .sel(comparator_1_eq));
  Clock clock_1 (.out(clock_1_out));
  ROM rom_1 (.addr(register_1_q), .data({instruction, dir_A, dir_b}));
  nor nor_1 (nor_1_out, RAM_WRITE, no_reg);
  Clock clock_2 (.out(clock_2_out));
  register_bank_8 register_bank_8_1 (
    .clock_reg(clock_2_out), .reset_reg(reset), .enable(nor_1_out), .dir_DATO(dir_A),
    .dato(multiplexer_3_out), .dir_A(dir_A), .dir_B(dir_b), .ope_A(opeA), .R7(pointer_R7),
    .ope_B(register_bank_8_1_ope_b));
  Multiplexer #(.select(3), .width(8)) multiplexer_3 (
    .in0(and_2_out), .in1(or_1_out), .in2(adder_2_out), .in3(register_bank_8_1_ope_b),
    .in4(multiplexer_4_out), .in5(multiplexer_5_out), .in7(ram_1_dout), .out(multiplexer_3_out),
    .sel(instruction));  // open: in6
  assign and_2_out = opeA & register_bank_8_1_ope_b;  // AND_Gate and_2, 8 bits wide
  assign or_1_out = opeA | register_bank_8_1_ope_b;  // OR_Gate or_1, 8 bits wide
  Adder adder_2 (.a(register_bank_8_1_ope_b), .b(opeA), .out(adder_2_out));  // open: cin, cout
  Button button_1 (.out(reset));
  Multiplexer #(.select(2), .width(8)) multiplexer_4 (
    .in0({opeA[6:0], 1'b0}), .in1({1'b0, opeA[7:1]}), .in2({opeA[6:0], opeA[7]}), .in3({opeA[0], opeA[7:1]}),
    .out(multiplexer_4_out), .sel(dir_b));
  and and_3 (RAM_WRITE, dir_b[0], instruction[5], instruction[6], instruction[7]);
  Clock clock_3 (.out(clock_3_out));
  assign not_1_out = ~opeA;  // NOT_Gate not_1, 8 bits wide
  Multiplexer #(.select(2), .width(8)) multiplexer_5 (
    .in0(not_1_out), .in1({8{1'b0}}), .in2({8{1'b1}}), .in3({opeA[3:0], opeA[7:4]}), .out(multiplexer_5_out),
    .sel(dir_b));
  RAM #(.asyncread("true"), .\type ("nonvolatile")) ram_1 (
    .addr(pointer_R7), .we(RAM_WRITE), .oe(1'b1), .clk(clock_3_out), .din(opeA), .dout(ram_1_dout));

  // Other names for the same wires on the sheet: instruction[4:0] = {dir_A, dir_b}; R_W = dir_b[0];
  //   step_5[4:0] = {dir_A, dir_b}; operation[2:0] = instruction

  // Notes on the sheet:
  //   contents of rom_1 (hex, n*v repeats v):
  //   a0 a6 81 81 84 84 84 a3 a0 a4 49 6c 2e b0 13 b3 8f 92 a1 c2 c0 bc bc 7e f8 5e f1 c1
endmodule

module compu_6_1 (
);

  wire clock_1_out, clock_2_out, clock_3_out, comparator_1_eq, no_reg, nor_1_out, RAM_WRITE, reset;
  wire [1:0] dir_b;
  wire [2:0] dir_A, xnor_1_out;
  wire [7:0] adder_1_out, adder_2_out, and_2_out, multiplexer_1_out, multiplexer_2_out, multiplexer_3_out,
       multiplexer_4_out, multiplexer_5_out, not_1_out, opeA, or_1_out, pointer_R7, Prog_Counter,
       register_bank_8_1_ope_b;
  wire [7:5] instruction;

  assign xnor_1_out = ~(instruction ^ 3'b110);  // XNOR_Gate xnor_1, 3 bits wide
  and and_1 (no_reg, xnor_1_out[2], xnor_1_out[1], xnor_1_out[0]);
  nor nor_1 (nor_1_out, RAM_WRITE, no_reg);
  Clock clock_1 (.out(clock_1_out));
  Multiplexer #(.width(8)) multiplexer_1 (
    .in0(8'h1), .in1({3'b000, dir_A, dir_b}), .out(multiplexer_1_out), .sel(no_reg));
  register_bank_8 register_bank_8_1 (
    .clock_reg(clock_1_out), .reset_reg(reset), .enable(nor_1_out), .dir_DATO(dir_A),
    .dato(multiplexer_2_out), .dir_A(dir_A), .dir_B(dir_b), .ope_A(opeA), .R7(pointer_R7),
    .ope_B(register_bank_8_1_ope_b));
  Multiplexer #(.select(3), .width(8)) multiplexer_2 (
    .in0(and_2_out), .in1(or_1_out), .in2(adder_2_out), .in3(register_bank_8_1_ope_b),
    .in4(multiplexer_4_out), .in5(multiplexer_5_out), .in7({instruction, dir_A, dir_b}),
    .out(multiplexer_2_out), .sel(instruction));  // open: in6
  Adder adder_1 (.a(Prog_Counter), .b(multiplexer_1_out), .out(adder_1_out));  // open: cin, cout
  Comparator comparator_1 (.a(8'hc1), .b({instruction, dir_A, dir_b}), .eq(comparator_1_eq));  // open: gt, lt
  assign and_2_out = opeA & register_bank_8_1_ope_b;  // AND_Gate and_2, 8 bits wide
  display_8bits display_8bits_1 (.in_1(Prog_Counter));
  Register register_1 (.D(multiplexer_3_out), .clk(clock_2_out), .Q(Prog_Counter), .clr(reset));  // open: en
  Multiplexer #(.width(8)) multiplexer_3 (
    .in0(adder_1_out), .in1(pointer_R7), .out(multiplexer_3_out), .sel(comparator_1_eq));
  Clock clock_2 (.out(clock_2_out));
  assign or_1_out = opeA | register_bank_8_1_ope_b;  // OR_Gate or_1, 8 bits wide
  Adder adder_2 (.a(register_bank_8_1_ope_b), .b(opeA), .out(adder_2_out));  // open: cin, cout
  Button button_1 (.out(reset));
  Multiplexer #(.select(2), .width(8)) multiplexer_4 (
    .in0({opeA[6:0], 1'b0}), .in1({1'b0, opeA[7:1]}), .in2({opeA[6:0], opeA[7]}), .in3({opeA[0], opeA[7:1]}),
    .out(multiplexer_4_out), .sel(dir_b));
  and and_3 (RAM_WRITE, dir_b[0], instruction[5], instruction[6], instruction[7]);
  Clock clock_3 (.out(clock_3_out));
  assign not_1_out = ~opeA;  // NOT_Gate not_1, 8 bits wide
  Multiplexer #(.select(2), .width(8)) multiplexer_5 (
    .in0(not_1_out), .in1({8{1'b0}}), .in2({8{1'b1}}), .in3({opeA[3:0], opeA[7:4]}), .out(multiplexer_5_out),
    .sel(dir_b));
  RAM #(.asyncread("true"), .\type ("nonvolatile")) ram_1 (
    .addr(Prog_Counter), .we(RAM_WRITE), .oe(1'b1), .clk(clock_3_out), .din(opeA),
    .dout({instruction, dir_A, dir_b}));

  // Other names for the same wires on the sheet: instruction[4:0] = {dir_A, dir_b};
  //   mem_reg[7:0] = {instruction, dir_A, dir_b}; R_W = dir_b[0]; step_5[4:0] = {dir_A, dir_b};
  //   operation[2:0] = instruction
endmodule

module compu_6_2 (
);

  wire clock_1_out, clock_2_out, clock_3_out, comparator_1_eq, no_reg, nor_1_out, RAM_WRITE, reset;
  wire [1:0] dir_b;
  wire [2:0] dir_A, xnor_1_out;
  wire [7:0] adder_1_out, adder_2_out, and_2_out, multiplexer_1_out, multiplexer_2_out, multiplexer_3_out,
       multiplexer_4_out, multiplexer_5_out, multiplexer_6_out, not_1_out, opeA, or_1_out, pointer_R7,
       Prog_Counter, register_bank_8_1_ope_b;
  wire [7:5] instruction;

  assign xnor_1_out = ~(instruction ^ 3'b110);  // XNOR_Gate xnor_1, 3 bits wide
  and and_1 (no_reg, xnor_1_out[2], xnor_1_out[1], xnor_1_out[0]);
  nor nor_1 (nor_1_out, RAM_WRITE, no_reg);
  Clock clock_1 (.out(clock_1_out));
  Multiplexer #(.width(8)) multiplexer_1 (
    .in0(8'h1), .in1({3'b000, dir_A, dir_b}), .out(multiplexer_1_out), .sel(no_reg));
  register_bank_8 register_bank_8_1 (
    .clock_reg(clock_1_out), .reset_reg(reset), .enable(nor_1_out), .dir_DATO(dir_A),
    .dato(multiplexer_2_out), .dir_A(dir_A), .dir_B(dir_b), .ope_A(opeA), .R7(pointer_R7),
    .ope_B(register_bank_8_1_ope_b));
  Multiplexer #(.select(3), .width(8)) multiplexer_2 (
    .in0(and_2_out), .in1(or_1_out), .in2(adder_2_out), .in3(register_bank_8_1_ope_b),
    .in4(multiplexer_4_out), .in5(multiplexer_5_out), .in7({instruction, dir_A, dir_b}),
    .out(multiplexer_2_out), .sel(instruction));  // open: in6
  Adder adder_1 (.a(Prog_Counter), .b(multiplexer_1_out), .out(adder_1_out));  // open: cin, cout
  Comparator comparator_1 (.a(8'hc1), .b({instruction, dir_A, dir_b}), .eq(comparator_1_eq));  // open: gt, lt
  assign and_2_out = opeA & register_bank_8_1_ope_b;  // AND_Gate and_2, 8 bits wide
  display_8bits display_8bits_1 (.in_1(Prog_Counter));
  Register register_1 (.D(multiplexer_3_out), .clk(clock_2_out), .Q(Prog_Counter), .clr(reset));  // open: en
  Multiplexer #(.width(8)) multiplexer_3 (
    .in0(adder_1_out), .in1(pointer_R7), .out(multiplexer_3_out), .sel(comparator_1_eq));
  Clock clock_2 (.out(clock_2_out));
  assign or_1_out = opeA | register_bank_8_1_ope_b;  // OR_Gate or_1, 8 bits wide
  Adder adder_2 (.a(register_bank_8_1_ope_b), .b(opeA), .out(adder_2_out));  // open: cin, cout
  Button button_1 (.out(reset));
  Multiplexer #(.select(2), .width(8)) multiplexer_4 (
    .in0({opeA[6:0], 1'b0}), .in1({1'b0, opeA[7:1]}), .in2({opeA[6:0], opeA[7]}), .in3({opeA[0], opeA[7:1]}),
    .out(multiplexer_4_out), .sel(dir_b));
  and and_3 (RAM_WRITE, dir_b[0], instruction[5], instruction[6], instruction[7]);
  Clock clock_3 (.out(clock_3_out));
  assign not_1_out = ~opeA;  // NOT_Gate not_1, 8 bits wide
  Multiplexer #(.select(2), .width(8)) multiplexer_5 (
    .in0(not_1_out), .in1({8{1'b0}}), .in2({8{1'b1}}), .in3({opeA[3:0], opeA[7:4]}), .out(multiplexer_5_out),
    .sel(dir_b));
  Multiplexer #(.width(8)) multiplexer_6 (.in0(Prog_Counter), .in1(pointer_R7), .out(multiplexer_6_out), .sel(no_reg));
  RAM #(.asyncread("true"), .\type ("nonvolatile")) ram_1 (
    .addr(multiplexer_6_out), .we(RAM_WRITE), .oe(1'b1), .clk(clock_3_out), .din(opeA),
    .dout({instruction, dir_A, dir_b}));

  // Other names for the same wires on the sheet: instruction[4:0] = {dir_A, dir_b};
  //   mem_reg[7:0] = {instruction, dir_A, dir_b}; R_W = dir_b[0]; step_5[4:0] = {dir_A, dir_b};
  //   operation[2:0] = instruction
endmodule

module compu_6_3 (
);

  wire and_1_out, clock_1_out, clock_2_out, clock_3_out, clock_4_out, clock_5_out, comparator_1_eq,
       comparator_2_eq, GO_1, GO_2, GO_3, GO_4, no_reg, nor_1_out, RAM_WRITE, reset;
  wire [1:0] adder_2_out, dir_b, mini_instr_counter_q, multiplexer_4_out;
  wire [2:0] dir_A, xnor_1_out;
  wire [7:0] adder_1_out, adder_3_out, and_3_out, mem_reg, multiplexer_1_out, multiplexer_2_out,
       multiplexer_3_out, multiplexer_5_out, multiplexer_6_out, not_1_out, opeA, or_1_out, pointer_R7,
       program_counter, register_bank_8_1_ope_b;
  wire [7:5] instruction;

  and and_1 (and_1_out, GO_2, nor_1_out);
  assign xnor_1_out = ~(instruction ^ 3'b110);  // XNOR_Gate xnor_1, 3 bits wide
  nor nor_1 (nor_1_out, RAM_WRITE, no_reg);
  Clock clock_1 (.out(clock_1_out));
  and and_2 (no_reg, xnor_1_out[2], xnor_1_out[1], xnor_1_out[0]);
  register_bank_8 register_bank_8_1 (
    .clock_reg(clock_1_out), .reset_reg(reset), .enable(and_1_out), .dir_DATO(dir_A),
    .dato(multiplexer_1_out), .dir_A(dir_A), .dir_B(dir_b), .ope_A(opeA), .R7(pointer_R7),
    .ope_B(register_bank_8_1_ope_b));
  Multiplexer #(.select(3), .width(8)) multiplexer_1 (
    .in0(and_3_out), .in1(or_1_out), .in2(adder_3_out), .in3(register_bank_8_1_ope_b),
    .in4(multiplexer_5_out), .in5(multiplexer_6_out), .in7(mem_reg), .out(multiplexer_1_out),
    .sel(instruction));  // open: in6
  Adder adder_1 (.a(program_counter), .b(multiplexer_2_out), .out(adder_1_out));  // open: cin, cout
  Multiplexer #(.width(8)) multiplexer_2 (
    .in0(8'h1), .in1({3'b000, dir_A, dir_b}), .out(multiplexer_2_out), .sel(no_reg));
  assign and_3_out = opeA & register_bank_8_1_ope_b;  // AND_Gate and_3, 8 bits wide
  Multiplexer #(.width(8)) multiplexer_3 (
    .in0(adder_1_out), .in1(pointer_R7), .out(multiplexer_3_out), .sel(comparator_1_eq));
  Comparator comparator_1 (.a(8'hc1), .b({instruction, dir_A, dir_b}), .eq(comparator_1_eq));  // open: gt, lt
  Adder #(.width(2)) adder_2 (.a(mini_instr_counter_q), .b(2'b01), .out(adder_2_out));  // open: cin, cout
  Comparator #(.width(2)) comparator_2 (.a(mini_instr_counter_q), .b(2'b01), .eq(comparator_2_eq));  // open: gt, lt
  assign or_1_out = opeA | register_bank_8_1_ope_b;  // OR_Gate or_1, 8 bits wide
  display_8bits display_8bits_1 (.in_1(program_counter));
  Clock clock_2 (.out(clock_2_out));
  Register #(.width(2)) mini_instr_counter (
    .D(multiplexer_4_out), .clk(clock_3_out), .Q(mini_instr_counter_q), .clr(reset));  // open: en
  Multiplexer #(.width(2)) multiplexer_4 (
    .in0(adder_2_out), .in1(2'b00), .out(multiplexer_4_out), .sel(comparator_2_eq));
  Clock clock_3 (.out(clock_3_out));
  Adder adder_3 (.a(register_bank_8_1_ope_b), .b(opeA), .out(adder_3_out));  // open: cin, cout
  Register register_1 (.D(multiplexer_3_out), .en(GO_2), .clk(clock_2_out), .Q(program_counter), .clr(reset));
  Button button_1 (.out(reset));
  Multiplexer #(.select(2), .width(8)) multiplexer_5 (
    .in0({opeA[6:0], 1'b0}), .in1({1'b0, opeA[7:1]}), .in2({opeA[6:0], opeA[7]}), .in3({opeA[0], opeA[7:1]}),
    .out(multiplexer_5_out), .sel(dir_b));
  Decoder #(.select(2)) decoder_1 (
    .out0(GO_1), .out1(GO_2), .out2(GO_3), .out3(GO_4), .sel(mini_instr_counter_q));  // open: en
  and and_4 (RAM_WRITE, dir_b[0], instruction[5], instruction[6], instruction[7]);
  Clock clock_4 (.out(clock_4_out));
  Register IR (.D(mem_reg), .en(GO_1), .clk(clock_5_out), .Q({instruction, dir_A, dir_b}), .clr(reset));
  Clock clock_5 (.out(clock_5_out));
  assign not_1_out = ~opeA;  // NOT_Gate not_1, 8 bits wide
  Multiplexer #(.select(2), .width(8)) multiplexer_6 (
    .in0(not_1_out), .in1({8{1'b0}}), .in2({8{1'b1}}), .in3({opeA[3:0], opeA[7:4]}), .out(multiplexer_6_out),
    .sel(dir_b));
  RAM #(.asyncread("true"), .\type ("nonvolatile")) ram_1 (
    .addr(program_counter), .we(RAM_WRITE), .oe(1'b1), .clk(clock_4_out), .din(opeA), .dout(mem_reg));

  // Other names for the same wires on the sheet: instruction[4:0] = {dir_A, dir_b}; R_W = dir_b[0];
  //   step_5[4:0] = {dir_A, dir_b}; operation[2:0] = instruction
endmodule

module compu_6_4 (
);

  wire and_1_out, and_5_out, clock_1_out, clock_2_out, clock_3_out, clock_4_out, clock_5_out,
       comparator_1_eq, comparator_2_eq, GO_1, GO_2, GO_3, GO_4, no_reg, nor_1_out, RAM_WRITE, reset;
  wire [1:0] adder_2_out, dir_b, mini_instr_counter_q, multiplexer_4_out;
  wire [2:0] dir_A, xnor_1_out, xnor_2_out;
  wire [7:0] adder_1_out, adder_3_out, and_3_out, mem_reg, multiplexer_1_out, multiplexer_2_out,
       multiplexer_3_out, multiplexer_5_out, multiplexer_6_out, multiplexer_7_out, not_1_out, opeA, or_1_out,
       pointer_R7, program_counter, register_bank_8_1_ope_b;
  wire [7:5] instruction;

  and and_1 (and_1_out, GO_2, nor_1_out);
  assign xnor_1_out = ~(instruction ^ 3'b110);  // XNOR_Gate xnor_1, 3 bits wide
  nor nor_1 (nor_1_out, RAM_WRITE, no_reg);
  Clock clock_1 (.out(clock_1_out));
  and and_2 (no_reg, xnor_1_out[2], xnor_1_out[1], xnor_1_out[0]);
  register_bank_8 register_bank_8_1 (
    .clock_reg(clock_1_out), .reset_reg(reset), .enable(and_1_out), .dir_DATO(dir_A),
    .dato(multiplexer_1_out), .dir_A(dir_A), .dir_B(dir_b), .ope_A(opeA), .R7(pointer_R7),
    .ope_B(register_bank_8_1_ope_b));
  Multiplexer #(.select(3), .width(8)) multiplexer_1 (
    .in0(and_3_out), .in1(or_1_out), .in2(adder_3_out), .in3(register_bank_8_1_ope_b),
    .in4(multiplexer_5_out), .in5(multiplexer_6_out), .in7(mem_reg), .out(multiplexer_1_out),
    .sel(instruction));  // open: in6
  Adder adder_1 (.a(program_counter), .b(multiplexer_2_out), .out(adder_1_out));  // open: cin, cout
  Multiplexer #(.width(8)) multiplexer_2 (
    .in0(8'h1), .in1({3'b000, dir_A, dir_b}), .out(multiplexer_2_out), .sel(no_reg));
  assign and_3_out = opeA & register_bank_8_1_ope_b;  // AND_Gate and_3, 8 bits wide
  Multiplexer #(.width(8)) multiplexer_3 (
    .in0(adder_1_out), .in1(pointer_R7), .out(multiplexer_3_out), .sel(comparator_1_eq));
  Comparator comparator_1 (.a(8'hc1), .b({instruction, dir_A, dir_b}), .eq(comparator_1_eq));  // open: gt, lt
  Adder #(.width(2)) adder_2 (.a(mini_instr_counter_q), .b(2'b01), .out(adder_2_out));  // open: cin, cout
  Comparator #(.width(2)) comparator_2 (.a(mini_instr_counter_q), .b(2'b01), .eq(comparator_2_eq));  // open: gt, lt
  assign or_1_out = opeA | register_bank_8_1_ope_b;  // OR_Gate or_1, 8 bits wide
  display_8bits display_8bits_1 (.in_1(program_counter));
  Clock clock_2 (.out(clock_2_out));
  Register #(.width(2)) mini_instr_counter (
    .D(multiplexer_4_out), .clk(clock_3_out), .Q(mini_instr_counter_q), .clr(reset));  // open: en
  Multiplexer #(.width(2)) multiplexer_4 (
    .in0(adder_2_out), .in1(2'b00), .out(multiplexer_4_out), .sel(comparator_2_eq));
  Clock clock_3 (.out(clock_3_out));
  Adder adder_3 (.a(register_bank_8_1_ope_b), .b(opeA), .out(adder_3_out));  // open: cin, cout
  Register register_1 (.D(multiplexer_3_out), .en(GO_2), .clk(clock_2_out), .Q(program_counter), .clr(reset));
  Button button_1 (.out(reset));
  Multiplexer #(.select(2), .width(8)) multiplexer_5 (
    .in0({opeA[6:0], 1'b0}), .in1({1'b0, opeA[7:1]}), .in2({opeA[6:0], opeA[7]}), .in3({opeA[0], opeA[7:1]}),
    .out(multiplexer_5_out), .sel(dir_b));
  Decoder #(.select(2)) decoder_1 (
    .out0(GO_1), .out1(GO_2), .out2(GO_3), .out3(GO_4), .sel(mini_instr_counter_q));  // open: en
  and and_4 (RAM_WRITE, dir_b[0], instruction[5], instruction[6], instruction[7]);
  Clock clock_4 (.out(clock_4_out));
  Register IR (.D(mem_reg), .en(GO_1), .clk(clock_5_out), .Q({instruction, dir_A, dir_b}), .clr(reset));
  Clock clock_5 (.out(clock_5_out));
  assign not_1_out = ~opeA;  // NOT_Gate not_1, 8 bits wide
  Multiplexer #(.select(2), .width(8)) multiplexer_6 (
    .in0(not_1_out), .in1({8{1'b0}}), .in2({8{1'b1}}), .in3({opeA[3:0], opeA[7:4]}), .out(multiplexer_6_out),
    .sel(dir_b));
  Multiplexer #(.width(8)) multiplexer_7 (
    .in0(program_counter), .in1(pointer_R7), .out(multiplexer_7_out), .sel(and_5_out));
  RAM #(.asyncread("true"), .\type ("nonvolatile")) ram_1 (
    .addr(multiplexer_7_out), .we(RAM_WRITE), .oe(1'b1), .clk(clock_4_out), .din(opeA), .dout(mem_reg));
  assign xnor_2_out = ~(instruction ^ 3'b111);  // XNOR_Gate xnor_2, 3 bits wide
  and and_5 (and_5_out, xnor_2_out[2], xnor_2_out[1], xnor_2_out[0]);

  // Other names for the same wires on the sheet: instruction[4:0] = {dir_A, dir_b}; R_W = dir_b[0];
  //   step_5[4:0] = {dir_A, dir_b}; operation[2:0] = instruction
endmodule

module compu_6_5 (
);

  wire and_1_out, and_5_out, clock_1_out, clock_2_out, clock_3_out, clock_4_out, clock_5_out,
       comparator_1_eq, comparator_2_eq, GO_1, GO_2, GO_3, GO_4, no_reg, nor_1_out, RAM_WRITE, reset;
  wire [1:0] adder_2_out, dir_b, mini_instr_counter_q, multiplexer_4_out;
  wire [2:0] dir_A, xnor_1_out, xnor_2_out;
  wire [7:0] adder_1_out, adder_3_out, and_3_out, mem_reg, multiplexer_1_out, multiplexer_2_out,
       multiplexer_3_out, multiplexer_5_out, multiplexer_6_out, multiplexer_7_out, not_1_out, opeA, or_1_out,
       pointer_R7, program_counter, register_bank_8_1_ope_b;
  wire [7:5] instruction;

  and and_1 (and_1_out, GO_2, nor_1_out);
  assign xnor_1_out = ~(instruction ^ 3'b110);  // XNOR_Gate xnor_1, 3 bits wide
  nor nor_1 (nor_1_out, RAM_WRITE, no_reg);
  Clock clock_1 (.out(clock_1_out));
  and and_2 (no_reg, xnor_1_out[2], xnor_1_out[1], xnor_1_out[0]);
  register_bank_8 register_bank_8_1 (
    .clock_reg(clock_1_out), .reset_reg(reset), .enable(and_1_out), .dir_DATO(dir_A),
    .dato(multiplexer_1_out), .dir_A(dir_A), .dir_B(dir_b), .ope_A(opeA), .R7(pointer_R7),
    .ope_B(register_bank_8_1_ope_b));
  Multiplexer #(.select(3), .width(8)) multiplexer_1 (
    .in0(and_3_out), .in1(or_1_out), .in2(adder_3_out), .in3(register_bank_8_1_ope_b),
    .in4(multiplexer_5_out), .in5(multiplexer_6_out), .in7(mem_reg), .out(multiplexer_1_out),
    .sel(instruction));  // open: in6
  Adder adder_1 (.a(program_counter), .b(multiplexer_2_out), .out(adder_1_out));  // open: cin, cout
  Multiplexer #(.width(8)) multiplexer_2 (
    .in0(8'h1), .in1({3'b000, dir_A, dir_b}), .out(multiplexer_2_out), .sel(no_reg));
  assign and_3_out = opeA & register_bank_8_1_ope_b;  // AND_Gate and_3, 8 bits wide
  Multiplexer #(.width(8)) multiplexer_3 (
    .in0(adder_1_out), .in1(pointer_R7), .out(multiplexer_3_out), .sel(comparator_1_eq));
  Comparator comparator_1 (.a(8'hc1), .b({instruction, dir_A, dir_b}), .eq(comparator_1_eq));  // open: gt, lt
  Adder #(.width(2)) adder_2 (.a(mini_instr_counter_q), .b(2'b01), .out(adder_2_out));  // open: cin, cout
  Comparator #(.width(2)) comparator_2 (.a(mini_instr_counter_q), .b(2'b01), .eq(comparator_2_eq));  // open: gt, lt
  assign or_1_out = opeA | register_bank_8_1_ope_b;  // OR_Gate or_1, 8 bits wide
  display_8bits display_8bits_1 (.in_1(program_counter));
  Clock clock_2 (.out(clock_2_out));
  Register #(.width(2)) mini_instr_counter (
    .D(multiplexer_4_out), .clk(clock_3_out), .Q(mini_instr_counter_q), .clr(reset));  // open: en
  Multiplexer #(.width(2)) multiplexer_4 (
    .in0(adder_2_out), .in1(2'b00), .out(multiplexer_4_out), .sel(comparator_2_eq));
  Clock clock_3 (.out(clock_3_out));
  Adder adder_3 (.a(register_bank_8_1_ope_b), .b(opeA), .out(adder_3_out));  // open: cin, cout
  Register register_1 (.D(multiplexer_3_out), .en(GO_1), .clk(clock_2_out), .Q(program_counter), .clr(reset));
  Button button_1 (.out(reset));
  Multiplexer #(.select(2), .width(8)) multiplexer_5 (
    .in0({opeA[6:0], 1'b0}), .in1({1'b0, opeA[7:1]}), .in2({opeA[6:0], opeA[7]}), .in3({opeA[0], opeA[7:1]}),
    .out(multiplexer_5_out), .sel(dir_b));
  Decoder #(.select(2)) decoder_1 (
    .out0(GO_1), .out1(GO_2), .out2(GO_3), .out3(GO_4), .sel(mini_instr_counter_q));  // open: en
  and and_4 (RAM_WRITE, dir_b[0], instruction[5], instruction[6], instruction[7]);
  Clock clock_4 (.out(clock_4_out));
  Register IR (.D(mem_reg), .en(GO_1), .clk(clock_5_out), .Q({instruction, dir_A, dir_b}), .clr(reset));
  Clock clock_5 (.out(clock_5_out));
  assign not_1_out = ~opeA;  // NOT_Gate not_1, 8 bits wide
  Multiplexer #(.select(2), .width(8)) multiplexer_6 (
    .in0(not_1_out), .in1({8{1'b0}}), .in2({8{1'b1}}), .in3({opeA[3:0], opeA[7:4]}), .out(multiplexer_6_out),
    .sel(dir_b));
  Multiplexer #(.width(8)) multiplexer_7 (
    .in0(program_counter), .in1(pointer_R7), .out(multiplexer_7_out), .sel(and_5_out));
  RAM #(.asyncread("true"), .\type ("nonvolatile")) ram_1 (
    .addr(multiplexer_7_out), .we(RAM_WRITE), .oe(1'b1), .clk(clock_4_out), .din(opeA), .dout(mem_reg));
  assign xnor_2_out = ~(instruction ^ 3'b111);  // XNOR_Gate xnor_2, 3 bits wide
  and and_5 (and_5_out, xnor_2_out[2], xnor_2_out[1], xnor_2_out[0]);

  // Other names for the same wires on the sheet: instruction[4:0] = {dir_A, dir_b}; R_W = dir_b[0];
  //   step_5[4:0] = {dir_A, dir_b}; operation[2:0] = instruction
endmodule

module compu_6_6 (
);

  wire and_1_out, and_5_out, clock_1_out, clock_2_out, clock_3_out, clock_4_out, clock_5_out,
       comparator_1_eq, comparator_2_eq, GO_1, GO_2, GO_3, GO_4, no_reg, nor_1_out, RAM_WRITE, reset;
  wire [1:0] adder_2_out, dir_b, mini_instr_counter_q, multiplexer_4_out;
  wire [2:0] dir_A, xnor_1_out, xnor_2_out;
  wire [7:0] adder_1_out, adder_3_out, and_3_out, mem_reg, multiplexer_1_out, multiplexer_2_out,
       multiplexer_3_out, multiplexer_5_out, multiplexer_6_out, multiplexer_7_out, not_1_out, opeA, or_1_out,
       pointer_R7, program_counter, register_bank_8_1_ope_b;
  wire [7:5] instruction;

  and and_1 (and_1_out, GO_2, nor_1_out);
  assign xnor_1_out = ~(instruction ^ 3'b110);  // XNOR_Gate xnor_1, 3 bits wide
  nor nor_1 (nor_1_out, RAM_WRITE, no_reg);
  Clock clock_1 (.out(clock_1_out));
  and and_2 (no_reg, xnor_1_out[2], xnor_1_out[1], xnor_1_out[0]);
  register_bank_8 register_bank_8_1 (
    .clock_reg(clock_1_out), .reset_reg(reset), .enable(and_1_out), .dir_DATO(dir_A),
    .dato(multiplexer_1_out), .dir_A(dir_A), .dir_B(dir_b), .ope_A(opeA), .R7(pointer_R7),
    .ope_B(register_bank_8_1_ope_b));
  Multiplexer #(.select(3), .width(8)) multiplexer_1 (
    .in0(and_3_out), .in1(or_1_out), .in2(adder_3_out), .in3(register_bank_8_1_ope_b),
    .in4(multiplexer_5_out), .in5(multiplexer_6_out), .in7(mem_reg), .out(multiplexer_1_out),
    .sel(instruction));  // open: in6
  Adder adder_1 (.a(program_counter), .b(multiplexer_2_out), .out(adder_1_out));  // open: cin, cout
  Multiplexer #(.width(8)) multiplexer_2 (
    .in0(8'h1), .in1({3'b000, dir_A, dir_b}), .out(multiplexer_2_out), .sel(no_reg));
  assign and_3_out = opeA & register_bank_8_1_ope_b;  // AND_Gate and_3, 8 bits wide
  Multiplexer #(.width(8)) multiplexer_3 (
    .in0(adder_1_out), .in1(pointer_R7), .out(multiplexer_3_out), .sel(comparator_1_eq));
  Comparator comparator_1 (.a(8'hc1), .b({instruction, dir_A, dir_b}), .eq(comparator_1_eq));  // open: gt, lt
  Adder #(.width(2)) adder_2 (.a(mini_instr_counter_q), .b(2'b01), .out(adder_2_out));  // open: cin, cout
  Comparator #(.width(2)) comparator_2 (.a(mini_instr_counter_q), .b(2'b01), .eq(comparator_2_eq));  // open: gt, lt
  assign or_1_out = opeA | register_bank_8_1_ope_b;  // OR_Gate or_1, 8 bits wide
  display_8bits display_8bits_1 (.in_1(program_counter));
  Clock clock_2 (.out(clock_2_out));
  Register #(.width(2)) mini_instr_counter (
    .D(multiplexer_4_out), .clk(clock_3_out), .Q(mini_instr_counter_q), .clr(reset));  // open: en
  Multiplexer #(.width(2)) multiplexer_4 (
    .in0(adder_2_out), .in1(2'b00), .out(multiplexer_4_out), .sel(comparator_2_eq));
  Clock clock_3 (.out(clock_3_out));
  Adder adder_3 (.a(register_bank_8_1_ope_b), .b(opeA), .out(adder_3_out));  // open: cin, cout
  Register register_1 (.D(multiplexer_3_out), .en(GO_2), .clk(clock_2_out), .Q(program_counter), .clr(reset));
  Button button_1 (.out(reset));
  Multiplexer #(.select(2), .width(8)) multiplexer_5 (
    .in0({opeA[6:0], 1'b0}), .in1({1'b0, opeA[7:1]}), .in2({opeA[6:0], opeA[7]}), .in3({opeA[0], opeA[7:1]}),
    .out(multiplexer_5_out), .sel(dir_b));
  Decoder #(.select(2)) decoder_1 (
    .out0(GO_1), .out1(GO_2), .out2(GO_3), .out3(GO_4), .sel(mini_instr_counter_q));  // open: en
  and and_4 (RAM_WRITE, dir_b[0], instruction[5], instruction[6], instruction[7]);
  Clock clock_4 (.out(clock_4_out));
  Register IR (.D(mem_reg), .en(GO_1), .clk(clock_5_out), .Q({instruction, dir_A, dir_b}), .clr(reset));
  Clock clock_5 (.out(clock_5_out));
  assign not_1_out = ~opeA;  // NOT_Gate not_1, 8 bits wide
  Multiplexer #(.select(2), .width(8)) multiplexer_6 (
    .in0(not_1_out), .in1({8{1'b0}}), .in2({8{1'b1}}), .in3({opeA[3:0], opeA[7:4]}), .out(multiplexer_6_out),
    .sel(dir_b));
  Multiplexer #(.width(8)) multiplexer_7 (
    .in0(program_counter), .in1(pointer_R7), .out(multiplexer_7_out), .sel(and_5_out));
  RAM #(.asyncread("true"), .\type ("nonvolatile")) ram_1 (
    .addr(multiplexer_7_out), .we(RAM_WRITE), .oe(1'b1), .clk(clock_4_out), .din(opeA), .dout(mem_reg));
  assign xnor_2_out = ~(instruction ^ 3'b111);  // XNOR_Gate xnor_2, 3 bits wide
  and and_5 (and_5_out, xnor_2_out[2], xnor_2_out[1], xnor_2_out[0], GO_2);

  // Other names for the same wires on the sheet: instruction[4:0] = {dir_A, dir_b}; R_W = dir_b[0];
  //   step_5[4:0] = {dir_A, dir_b}; operation[2:0] = instruction
endmodule

module compu_6_7 (
);

  wire and_1_out, and_5_out, clock_1_out, clock_2_out, clock_3_out, clock_4_out, clock_5_out,
       comparator_1_eq, comparator_2_eq, GO_1, GO_2, GO_3, GO_4, no_reg, nor_1_out, RAM_WRITE, reset;
  wire [1:0] adder_2_out, dir_b, mini_instr_counter_q, multiplexer_4_out;
  wire [2:0] dir_A, xnor_1_out, xnor_2_out;
  wire [7:0] adder_1_out, adder_3_out, and_3_out, mem_reg, multiplexer_1_out, multiplexer_2_out,
       multiplexer_3_out, multiplexer_5_out, multiplexer_6_out, multiplexer_7_out, not_1_out, opeA, or_1_out,
       pointer_R7, program_counter, register_bank_8_1_ope_b;
  wire [7:5] instruction;

  and and_1 (and_1_out, GO_2, nor_1_out);
  assign xnor_1_out = ~(instruction ^ 3'b110);  // XNOR_Gate xnor_1, 3 bits wide
  nor nor_1 (nor_1_out, RAM_WRITE, no_reg);
  Clock clock_1 (.out(clock_1_out));
  and and_2 (no_reg, xnor_1_out[2], xnor_1_out[1], xnor_1_out[0]);
  register_bank_8 register_bank_8_1 (
    .clock_reg(clock_1_out), .reset_reg(reset), .enable(and_1_out), .dir_DATO(dir_A),
    .dato(multiplexer_1_out), .dir_A(dir_A), .dir_B(dir_b), .ope_A(opeA), .R7(pointer_R7),
    .ope_B(register_bank_8_1_ope_b));
  Multiplexer #(.select(3), .width(8)) multiplexer_1 (
    .in0(and_3_out), .in1(or_1_out), .in2(adder_3_out), .in3(register_bank_8_1_ope_b),
    .in4(multiplexer_5_out), .in5(multiplexer_6_out), .in7(mem_reg), .out(multiplexer_1_out),
    .sel(instruction));  // open: in6
  Adder adder_1 (.a(program_counter), .b(multiplexer_2_out), .out(adder_1_out));  // open: cin, cout
  Multiplexer #(.width(8)) multiplexer_2 (
    .in0(8'h1), .in1({3'b000, dir_A, dir_b}), .out(multiplexer_2_out), .sel(no_reg));
  assign and_3_out = opeA & register_bank_8_1_ope_b;  // AND_Gate and_3, 8 bits wide
  Multiplexer #(.width(8)) multiplexer_3 (
    .in0(adder_1_out), .in1(pointer_R7), .out(multiplexer_3_out), .sel(comparator_1_eq));
  Comparator comparator_1 (.a(8'hc1), .b({instruction, dir_A, dir_b}), .eq(comparator_1_eq));  // open: gt, lt
  Adder #(.width(2)) adder_2 (.a(mini_instr_counter_q), .b(2'b01), .out(adder_2_out));  // open: cin, cout
  Comparator #(.width(2)) comparator_2 (.a(mini_instr_counter_q), .b(2'b01), .eq(comparator_2_eq));  // open: gt, lt
  assign or_1_out = opeA | register_bank_8_1_ope_b;  // OR_Gate or_1, 8 bits wide
  display_8bits display_8bits_1 (.in_1(program_counter));
  Clock clock_2 (.out(clock_2_out));
  Register #(.width(2)) mini_instr_counter (
    .D(multiplexer_4_out), .clk(clock_3_out), .Q(mini_instr_counter_q), .clr(reset));  // open: en
  Multiplexer #(.width(2)) multiplexer_4 (
    .in0(adder_2_out), .in1(2'b00), .out(multiplexer_4_out), .sel(comparator_2_eq));
  Clock clock_3 (.out(clock_3_out));
  Adder adder_3 (.a(register_bank_8_1_ope_b), .b(opeA), .out(adder_3_out));  // open: cin, cout
  Register register_1 (.D(multiplexer_3_out), .en(GO_2), .clk(clock_2_out), .Q(program_counter), .clr(reset));
  Button button_1 (.out(reset));
  Multiplexer #(.select(2), .width(8)) multiplexer_5 (
    .in0({opeA[6:0], 1'b0}), .in1({1'b0, opeA[7:1]}), .in2({opeA[6:0], opeA[7]}), .in3({opeA[0], opeA[7:1]}),
    .out(multiplexer_5_out), .sel(dir_b));
  Decoder #(.select(2)) decoder_1 (
    .out0(GO_1), .out1(GO_2), .out2(GO_3), .out3(GO_4), .sel(mini_instr_counter_q));  // open: en
  and and_4 (RAM_WRITE, dir_b[0], instruction[5], instruction[6], instruction[7], GO_2);
  Clock clock_4 (.out(clock_4_out));
  Register IR (.D(mem_reg), .en(GO_1), .clk(clock_5_out), .Q({instruction, dir_A, dir_b}), .clr(reset));
  Clock clock_5 (.out(clock_5_out));
  assign not_1_out = ~opeA;  // NOT_Gate not_1, 8 bits wide
  Multiplexer #(.select(2), .width(8)) multiplexer_6 (
    .in0(not_1_out), .in1({8{1'b0}}), .in2({8{1'b1}}), .in3({opeA[3:0], opeA[7:4]}), .out(multiplexer_6_out),
    .sel(dir_b));
  Multiplexer #(.width(8)) multiplexer_7 (
    .in0(program_counter), .in1(pointer_R7), .out(multiplexer_7_out), .sel(and_5_out));
  RAM #(.asyncread("true"), .\type ("nonvolatile")) ram_1 (
    .addr(multiplexer_7_out), .we(RAM_WRITE), .oe(1'b1), .clk(clock_4_out), .din(opeA), .dout(mem_reg));
  assign xnor_2_out = ~(instruction ^ 3'b111);  // XNOR_Gate xnor_2, 3 bits wide
  and and_5 (and_5_out, xnor_2_out[2], xnor_2_out[1], xnor_2_out[0], GO_2);

  // Other names for the same wires on the sheet: instruction[4:0] = {dir_A, dir_b}; R_W = dir_b[0];
  //   step_5[4:0] = {dir_A, dir_b}; operation[2:0] = instruction
endmodule

module compu_7_1 (
);

  wire and_1_out, and_3_out, and_7_out, clock_1_out, clock_2_out, clock_3_out, clock_4_out, clock_5_out,
       comparator_1_eq, comparator_2_eq, comparator_3_eq, decoder_1_out1, GO_1, GO_2, GO_3, GO_4, halt,
       IR_enable, JUMP_op, MEM_op, need_1, nor_1_out, not_2_out, not_4_out, or_1_out, or_3_out, PC_enable,
       RAM_WRITE, reset;
  wire [1:0] adder_2_out, dir_b, mini_instr_counter_q, multiplexer_4_out, priority_encoder_1_out;
  wire [2:0] dir_A;
  wire [7:0] adder_1_out, adder_3_out, and_2_out, bit_extender_1_out, mem_reg, multiplexer_1_out,
       multiplexer_2_out, multiplexer_3_out, multiplexer_5_out, multiplexer_6_out, multiplexer_7_out,
       not_3_out, opeA, or_2_out, pointer_R7, program_counter, register_bank_8_1_ope_b, subtractor_1_out;
  wire [7:5] instruction;

  and and_1 (and_1_out, GO_1, nor_1_out);
  display_3bits display_3bits_1 (.in_1(dir_A));
  assign bit_extender_1_out = {{3{dir_A[2]}}, {dir_A, dir_b}};  // Bit_Extender bit_extender_1
  comp_3bits comp_3bits_1 (.N(instruction), .\ref (3'b110), .Y(JUMP_op));
  comp_3bits comp_3bits_2 (.N(instruction), .\ref (3'b111), .Y(MEM_op));
  nor nor_1 (nor_1_out, RAM_WRITE, JUMP_op);
  Clock clock_1 (.out(clock_1_out));
  Subtractor subtractor_1 (.a(bit_extender_1_out), .b(8'h1), .out(subtractor_1_out));  // open: bin, bout
  not not_1 (need_1, or_1_out);
  or or_1 (or_1_out, JUMP_op, MEM_op);
  register_bank_8 register_bank_8_1 (
    .clock_reg(clock_1_out), .reset_reg(reset), .enable(and_1_out), .dir_DATO(dir_A),
    .dato(multiplexer_1_out), .dir_A(dir_A), .dir_B(dir_b), .ope_A(opeA), .R7(pointer_R7),
    .ope_B(register_bank_8_1_ope_b));
  Multiplexer #(.select(3), .width(8)) multiplexer_1 (
    .in0(and_2_out), .in1(or_2_out), .in2(adder_3_out), .in3(register_bank_8_1_ope_b),
    .in4(multiplexer_5_out), .in5(multiplexer_6_out), .in7(mem_reg), .out(multiplexer_1_out),
    .sel(instruction));  // open: in6
  Multiplexer #(.width(8)) multiplexer_2 (.in0(8'h1), .in1(subtractor_1_out), .out(multiplexer_2_out), .sel(JUMP_op));
  Priority_Encoder #(.select(2)) priority_encoder_1 (
    .in0(need_1), .in1(or_1_out), .out(priority_encoder_1_out));  // open: in2, in3, gs, en_out, en_in
  assign and_2_out = opeA & register_bank_8_1_ope_b;  // AND_Gate and_2, 8 bits wide
  display_3bits display_3bits_2 (.in_1(instruction));
  Adder adder_1 (.a(program_counter), .b(multiplexer_2_out), .out(adder_1_out));  // open: cin, cout
  Multiplexer #(.width(8)) multiplexer_3 (
    .in0(adder_1_out), .in1(pointer_R7), .out(multiplexer_3_out), .sel(comparator_1_eq));
  Comparator comparator_1 (.a(8'hc1), .b({instruction, dir_A, dir_b}), .eq(comparator_1_eq));  // open: gt, lt
  and and_3 (and_3_out, GO_2, MEM_op);
  Adder #(.width(2)) adder_2 (.a(mini_instr_counter_q), .b(2'b01), .out(adder_2_out));  // open: cin, cout
  Multiplexer #(.width(2)) multiplexer_4 (
    .in0(adder_2_out), .in1(2'b00), .out(multiplexer_4_out), .sel(comparator_2_eq));
  Comparator #(.width(2)) comparator_2 (
    .a(mini_instr_counter_q), .b(priority_encoder_1_out), .eq(comparator_2_eq));  // open: gt, lt
  assign or_2_out = opeA | register_bank_8_1_ope_b;  // OR_Gate or_2, 8 bits wide
  Register #(.width(2)) mini_instr_counter (
    .D(multiplexer_4_out), .clk(clock_2_out), .Q(mini_instr_counter_q), .clr(reset));  // open: en
  Clock clock_2 (.out(clock_2_out));
  Adder adder_3 (.a(register_bank_8_1_ope_b), .b(opeA), .out(adder_3_out));  // open: cin, cout
  display_8bits display_8bits_1 (.in_1(program_counter));
  Register register_1 (.D(multiplexer_3_out), .en(PC_enable), .clk(clock_3_out), .Q(program_counter), .clr(reset));
  Clock clock_3 (.out(clock_3_out));
  or or_3 (or_3_out, need_1, JUMP_op, and_3_out);
  not not_2 (not_2_out, halt);
  display_2bits display_2bits_1 (.in_1(mini_instr_counter_q));
  Decoder #(.select(2)) decoder_1 (
    .out0(GO_1), .out1(decoder_1_out1), .out2(GO_3), .out3(GO_4), .sel(mini_instr_counter_q));  // open: en
  and and_4 (PC_enable, or_3_out, not_2_out);
  Comparator #(.mode("unsigned"), .width(5)) comparator_3 (
    .a({dir_A, dir_b}), .b({5{1'b0}}), .eq(comparator_3_eq));  // open: gt, lt
  Multiplexer #(.select(2), .width(8)) multiplexer_5 (
    .in0({opeA[6:0], 1'b0}), .in1({1'b0, opeA[7:1]}), .in2({opeA[6:0], opeA[7]}), .in3({opeA[0], opeA[7:1]}),
    .out(multiplexer_5_out), .sel(dir_b));
  Button button_1 (.out(reset));
  and and_5 (halt, comparator_3_eq, JUMP_op);
  or or_4 (GO_2, decoder_1_out1, need_1);
  and and_6 (RAM_WRITE, dir_b[0], instruction[5], instruction[6], instruction[7], GO_1);
  Clock clock_4 (.out(clock_4_out));
  assign not_3_out = ~opeA;  // NOT_Gate not_3, 8 bits wide
  Multiplexer #(.select(2), .width(8)) multiplexer_6 (
    .in0(not_3_out), .in1({8{1'b0}}), .in2({8{1'b1}}), .in3({opeA[3:0], opeA[7:4]}), .out(multiplexer_6_out),
    .sel(dir_b));
  Multiplexer #(.width(8)) multiplexer_7 (
    .in0(program_counter), .in1(pointer_R7), .out(multiplexer_7_out), .sel(and_7_out));
  RAM #(.asyncread("true"), .\type ("nonvolatile")) ram_1 (
    .addr(multiplexer_7_out), .we(RAM_WRITE), .oe(1'b1), .clk(clock_4_out), .din(opeA), .dout(mem_reg));
  Register IR (.D(mem_reg), .en(IR_enable), .clk(clock_5_out), .Q({instruction, dir_A, dir_b}), .clr(reset));
  Clock clock_5 (.out(clock_5_out));
  not not_4 (not_4_out, halt);
  display_8bits display_8bits_2 (.in_1(opeA));
  display_8bits display_8bits_3 (.in_1(mem_reg));
  and and_7 (and_7_out, MEM_op, GO_1);
  and and_8 (IR_enable, not_4_out, GO_2);
  display_8bits display_8bits_4 (.in_1(mem_reg));

  // Other names for the same wires on the sheet: operation[2:0] = instruction; instruction[4:0] = {dir_A, dir_b};
  //   R_W = dir_b[0]; step_5[4:0] = {dir_A, dir_b}
endmodule
