// Logisim project recup_viernes.circ as structural Verilog: 2 circuits, main circuit main
module main (
  input  [1:0] in_1,
  input  in_2,
  input  [1:0] in_3,
  input  [1:0] in_4,
  input  [1:0] in_5,
  input  [3:0] in_6,
  input  write_enable,
  input  [7:0] in_8,
  input  in_9,
  input  [1:0] address,
  input  [7:0] dato,
  input  [7:0] instruction,
  output out_13,
  output out_14,
  output [3:0] out_15
);

  wire button_1_out, button_2_out, button_3_out, button_4_out, button_5_out, button_6_out, button_7_out,
       clock_1_out, clock_2_out, clock_3_out, clock_4_out, decoder_1_out0, decoder_1_out1, decoder_2_out0,
       decoder_2_out1, decoder_2_out2, decoder_2_out3;
  wire [7:0] adder_1_out, adder_2_out, and_1_out, and_2_out, multiplexer_1_out, multiplexer_2_out, not_1_out,
       not_2_out, or_1_out, or_2_out, R0_q, R1_q, R2_q, R3_q, register_2_q, register_3_q,
       register_bank_1_ope_a, register_bank_1_ope_b, register_bank_2_ope_a, register_bank_2_ope_b;

  Button button_1 (.out(button_1_out));
  D_Flip_Flop d_ff_1 (
    .D(in_2), .clk(button_2_out), .Q(out_13), .Qn(out_14), .preset(button_1_out), .reset(button_3_out));
  Button button_2 (.out(button_2_out));
  Button button_3 (.out(button_3_out));
  Button button_4 (.out(button_4_out));
  Decoder decoder_1 (.out0(decoder_1_out0), .out1(decoder_1_out1), .sel(in_9));  // open: en
  Register #(.width(4)) register_1 (.D(in_6), .en(write_enable), .clk(button_4_out), .Q(out_15), .clr(button_5_out));
  Button button_5 (.out(button_5_out));
  Register register_2 (.D(in_8), .en(decoder_1_out0), .clk(clock_1_out), .Q(register_2_q));  // open: clr
  Register register_3 (.D(in_8), .en(decoder_1_out1), .clk(clock_1_out), .Q(register_3_q));  // open: clr
  Clock clock_1 (.out(clock_1_out));
  Decoder #(.select(2)) decoder_2 (
    .out0(decoder_2_out0), .out1(decoder_2_out1), .out2(decoder_2_out2), .out3(decoder_2_out3), .sel(address));  // open: en
  Register R0 (.D(dato), .en(decoder_2_out0), .clk(clock_2_out), .Q(R0_q));  // open: clr
  Register R1 (.D(dato), .en(decoder_2_out1), .clk(clock_2_out), .Q(R1_q));  // open: clr
  Register R2 (.D(dato), .en(decoder_2_out2), .clk(clock_2_out), .Q(R2_q));  // open: clr
  Register R3 (.D(dato), .en(decoder_2_out3), .clk(clock_2_out), .Q(R3_q));  // open: clr
  Clock clock_2 (.out(clock_2_out));
  Hex_Digit_Display hex_digit_display_1 (.value(register_2_q[7:4]));  // open: dp
  Hex_Digit_Display hex_digit_display_2 (.value(register_3_q[7:4]));  // open: dp
  Hex_Digit_Display hex_digit_display_3 (.value(register_2_q[3:0]));  // open: dp
  Hex_Digit_Display hex_digit_display_4 (.value(register_3_q[3:0]));  // open: dp
  Hex_Digit_Display hex_digit_display_5 (.value(R0_q[7:4]));  // open: dp
  Hex_Digit_Display hex_digit_display_6 (.value(R0_q[3:0]));  // open: dp
  Hex_Digit_Display hex_digit_display_7 (.value(R1_q[7:4]));  // open: dp
  Hex_Digit_Display hex_digit_display_8 (.value(R1_q[3:0]));  // open: dp
  Hex_Digit_Display hex_digit_display_9 (.value(R2_q[7:4]));  // open: dp
  Hex_Digit_Display hex_digit_display_10 (.value(R2_q[3:0]));  // open: dp
  Hex_Digit_Display hex_digit_display_11 (.value(R3_q[7:4]));  // open: dp
  Hex_Digit_Display hex_digit_display_12 (.value(R3_q[3:0]));  // open: dp
  Button button_6 (.out(button_6_out));
  Clock clock_3 (.out(clock_3_out));
  register_bank register_bank_1 (
    .WRITE_address(in_4), .clock_reg(clock_3_out), .reset_reg(button_6_out), .dato(multiplexer_1_out),
    .dir_A(in_1), .dir_B(in_3), .ope_A(register_bank_1_ope_a), .ope_B(register_bank_1_ope_b));
  Button button_7 (.out(button_7_out));
  assign not_1_out = ~register_bank_1_ope_b;  // NOT_Gate not_1, 8 bits wide
  Multiplexer #(.select(2), .width(8)) multiplexer_1 (
    .in0(not_1_out), .in1(and_1_out), .in2(or_1_out), .in3(adder_1_out), .out(multiplexer_1_out), .sel(in_5));
  Clock clock_4 (.out(clock_4_out));
  assign and_1_out = register_bank_1_ope_b & register_bank_1_ope_a;  // AND_Gate and_1, 8 bits wide
  Multiplexer #(.select(2), .width(8)) multiplexer_2 (
    .in0(not_2_out), .in1(and_2_out), .in2(or_2_out), .in3(adder_2_out), .out(multiplexer_2_out),
    .sel(instruction[3:2]));
  register_bank register_bank_2 (
    .WRITE_address(instruction[7:6]), .clock_reg(clock_4_out), .reset_reg(button_7_out),
    .dato(multiplexer_2_out), .dir_A(instruction[5:4]), .dir_B(instruction[1:0]),
    .ope_A(register_bank_2_ope_a), .ope_B(register_bank_2_ope_b));
  assign or_1_out = register_bank_1_ope_b | register_bank_1_ope_a;  // OR_Gate or_1, 8 bits wide
  assign not_2_out = ~register_bank_2_ope_b;  // NOT_Gate not_2, 8 bits wide
  assign and_2_out = register_bank_2_ope_b & register_bank_2_ope_a;  // AND_Gate and_2, 8 bits wide
  Adder adder_1 (.a(register_bank_1_ope_a), .b(register_bank_1_ope_b), .out(adder_1_out));  // open: cin, cout
  assign or_2_out = register_bank_2_ope_b | register_bank_2_ope_a;  // OR_Gate or_2, 8 bits wide
  Adder adder_2 (.a(register_bank_2_ope_a), .b(register_bank_2_ope_b), .out(adder_2_out));  // open: cin, cout

  // Other names for the same wires on the sheet: dir_b[1:0] = instruction[1:0]; operation[1:0] = instruction[3:2];
  //   dir_A[1:0] = instruction[5:4]; dir_RES[1:0] = instruction[7:6]
endmodule

module register_bank (
  input  [1:0] dir_A,
  input  [1:0] dir_B,
  input  [1:0] WRITE_address,
  input  [7:0] dato,
  input  clock_reg,
  input  reset_reg,
  output [7:0] ope_A,
  output [7:0] ope_B
);

  wire decoder_1_out0, decoder_1_out1, decoder_1_out2, decoder_1_out3;
  wire [3:0] binary_to_bcd_converter_1_p2, binary_to_bcd_converter_1_p3, binary_to_bcd_converter_1_p4,
       binary_to_bcd_converter_2_p2, binary_to_bcd_converter_2_p3, binary_to_bcd_converter_2_p4,
       binary_to_bcd_converter_3_p2, binary_to_bcd_converter_3_p3, binary_to_bcd_converter_3_p4,
       binary_to_bcd_converter_4_p2, binary_to_bcd_converter_4_p3, binary_to_bcd_converter_4_p4, R0_q,
       R0_q_2, R1_q, R1_q_2, R2_q, R2_q_2, R3_q, R3_q_2;

  Decoder #(.select(2)) decoder_1 (
    .out0(decoder_1_out0), .out1(decoder_1_out1), .out2(decoder_1_out2), .out3(decoder_1_out3),
    .sel(WRITE_address));  // open: en
  Register R3 (.D(dato), .en(decoder_1_out3), .clk(clock_reg), .Q({R3_q_2, R3_q}), .clr(reset_reg));
  Register R2 (.D(dato), .en(decoder_1_out2), .clk(clock_reg), .Q({R2_q_2, R2_q}), .clr(reset_reg));
  Register R1 (.D(dato), .en(decoder_1_out1), .clk(clock_reg), .Q({R1_q_2, R1_q}), .clr(reset_reg));
  Register R0 (.D(dato), .en(decoder_1_out0), .clk(clock_reg), .Q({R0_q_2, R0_q}), .clr(reset_reg));
  Hex_Digit_Display R3_hex_H (.value(R3_q_2));  // open: dp
  Hex_Digit_Display R2_hex_H (.value(R2_q_2));  // open: dp
  Hex_Digit_Display R1_hex_H (.value(R1_q_2));  // open: dp
  Hex_Digit_Display R0_hex_H (.value(R0_q_2));  // open: dp
  Hex_Digit_Display R3_hex_L (.value(R3_q));  // open: dp
  Hex_Digit_Display R2_hex_L (.value(R2_q));  // open: dp
  Hex_Digit_Display R1_hex_L (.value(R1_q));  // open: dp
  Hex_Digit_Display R0_hex_L (.value(R0_q));  // open: dp
  Hex_Digit_Display R3dec2 (.value(binary_to_bcd_converter_1_p2));  // open: dp
  // Binary_to_BCD_converter #(.binvalue(8)) binary_to_bcd_converter_1: pin names not known; wires that end beside it: {R3_q_2, R3_q}, binary_to_bcd_converter_1_p2, binary_to_bcd_converter_1_p3, binary_to_bcd_converter_1_p4
  Hex_Digit_Display R2dec2 (.value(binary_to_bcd_converter_2_p2));  // open: dp
  // Binary_to_BCD_converter #(.binvalue(8)) binary_to_bcd_converter_2: pin names not known; wires that end beside it: {R2_q_2, R2_q}, binary_to_bcd_converter_2_p2, binary_to_bcd_converter_2_p3, binary_to_bcd_converter_2_p4
  Hex_Digit_Display R1dec2 (.value(binary_to_bcd_converter_3_p2));  // open: dp
  // Binary_to_BCD_converter #(.binvalue(8)) binary_to_bcd_converter_3: pin names not known; wires that end beside it: {R1_q_2, R1_q}, binary_to_bcd_converter_3_p2, binary_to_bcd_converter_3_p3, binary_to_bcd_converter_3_p4
  Hex_Digit_Display R0dec2 (.value(binary_to_bcd_converter_4_p2));  // open: dp
  // Binary_to_BCD_converter #(.binvalue(8)) binary_to_bcd_converter_4: pin names not known; wires that end beside it: {R0_q_2, R0_q}, binary_to_bcd_converter_4_p2, binary_to_bcd_converter_4_p3, binary_to_bcd_converter_4_p4
  Hex_Digit_Display R3dec1 (.value(binary_to_bcd_converter_1_p3));  // open: dp
  Hex_Digit_Display R3dec0 (.value(binary_to_bcd_converter_1_p4));  // open: dp
  Hex_Digit_Display R2dec1 (.value(binary_to_bcd_converter_2_p3));  // open: dp
  Hex_Digit_Display R2dec0 (.value(binary_to_bcd_converter_2_p4));  // open: dp
  Hex_Digit_Display R1dec1 (.value(binary_to_bcd_converter_3_p3));  // open: dp
  Hex_Digit_Display R1dec0 (.value(binary_to_bcd_converter_3_p4));  // open: dp
  Hex_Digit_Display R0dec1 (.value(binary_to_bcd_converter_4_p3));  // open: dp
  Hex_Digit_Display R0dec0 (.value(binary_to_bcd_converter_4_p4));  // open: dp
  Multiplexer #(.select(2), .width(8)) multiplexer_1 (
    .in0({R0_q_2, R0_q}), .in1({R1_q_2, R1_q}), .in2({R2_q_2, R2_q}), .in3({R3_q_2, R3_q}), .out(ope_A),
    .sel(dir_A));
  Multiplexer #(.select(2), .width(8)) multiplexer_2 (
    .in0({R0_q_2, R0_q}), .in1({R1_q_2, R1_q}), .in2({R2_q_2, R2_q}), .in3({R3_q_2, R3_q}), .out(ope_B),
    .sel(dir_B));
endmodule
