// Logisim project Clase_1_Circuitos_Combinacionales.circ as structural Verilog: 11 circuits, main circuit main
module main (
  input  [3:0] in_1,
  input  [3:0] in_2,
  input  in_3,
  input  [3:0] in_4,
  input  [2:0] in_5,
  input  [3:0] in_6,
  input  [2:0] Entradas,
  input  [2:0] in_8,
  input  [3:0] in_9,
  input  [2:0] in_10,
  input  [3:0] in_11,
  input  [2:0] in_12,
  input  [3:0] in_13,
  input  [1:0] Selector,
  input  [3:0] in_15,
  input  [2:0] Entradas_2,
  input  [1:0] Selector_2,
  input  \Señal ,
  input  [1:0] Selector_3,
  input  [7:0] in_20,
  input  Valida_Salida,
  input  Entradas_3,
  input  in_23,
  input  [2:0] in_24,
  input  in_25,
  input  [4:0] in_26,
  input  [5:0] in_27,
  input  in_28,
  input  Habilitador,
  input  [7:0] in_30,
  input  [7:0] in_31,
  input  [7:0] in_32,
  input  [6:0] in_33,
  input  [7:0] in_34,
  input  in_35,
  input  in_36,
  input  in_37,
  input  [1:0] in_38,
  input  in_39,
  input  in_40,
  input  in_41,
  input  in_42,
  input  [7:0] in_43,
  input  [7:0] in_44,
  output [3:0] out_45,
  output [2:0] Salida,
  output [2:0] Salidas,
  output [4:0] out_48,
  output [2:0] out_49,
  output [2:0] out_50,
  output [2:0] out_51,
  output Salidas_2,
  output out_53,
  output out_54,
  output out_55,
  output [3:0] out_56,
  output [3:0] out_57,
  output [1:0] Salida_2,
  output [7:0] out_59,
  output Group_Select,
  output [23:0] out_61,
  output [1:0] Salida_3
);

  wire adder_1_cout, adder_2_cout, adder_3_cout, button_1_out, button_2_out;
  wire [2:0] adder_1_out, adder_2_out, bitadder_1_out, bitadder_2_out, bitadder_3_out, bitadder_4_out,
       bitadder_5_out, contador_unos_1_contador, seleccionador_color_1_x;
  wire [3:0] adder_3_out, bit_extender_1_out, bit_extender_2_out;
  wire [4:0] bit_extender_3_out, bit_extender_4_out;
  wire [6:0] convert_display7seg_1_convert;

  Seleccionador_Color seleccionador_color_1 (.a(in_5), .x(seleccionador_color_1_x));
  Multiplexer #(.select(2), .width(3)) multiplexer_1 (
    .in0(Entradas), .in1(in_8), .in2(in_10), .in3(in_12), .out(Salida), .sel(Selector));
  Demultiplexer #(.select(2), .width(3)) demultiplexer_1 (
    .out0(Salidas), .out1(out_49), .out2(out_50), .out3(out_51), .in(Entradas_2), .sel(Selector_2));
  Decoder #(.select(2)) decoder_1 (
    .out0(Salidas_2), .out1(out_53), .out2(out_54), .out3(out_55), .sel(Selector_3), .en(\Señal ));
  Priority_Encoder #(.select(2)) priority_encoder_1 (
    .in0(Entradas_3), .in1(in_23), .in2(in_25), .in3(in_28), .out(Salida_2), .gs(Group_Select),
    .en_out(Valida_Salida), .en_in(Habilitador));
  Circuito_Elector circuito_elector_1 (.SELL(in_3), .B(in_4), .A(in_1), .out_4(out_45));
  // RGBLED rgbled_1: pin names not known; wires that end beside it: seleccionador_color_1_x[2], seleccionador_color_1_x[1], seleccionador_color_1_x[0]
  BitSelector #(.group(2)) bitselector_1 (.in(in_34), .out(Salida_3), .sel(in_38));
  DotMatrix #(.matrixrows(4)) dotmatrix_1 (.col0(in_6), .col1(in_9), .col2(in_11), .col3(in_13), .col4(in_15));
  Button button_1 (.out(button_1_out));
  Logic_Gates logic_gates_1 (.A(in_39), .B(in_40));
  Reto_3 reto_3_1 (.in_1(in_43), .in_2(in_44));
  Contador_Unos contador_unos_1 (.Entrada(in_2), .Contador(contador_unos_1_contador));
  Nuevo_Bloque nuevo_bloque_1 (.Red(button_1_out), .Blue(button_2_out));
  Convert_Display7seg convert_display7seg_1 (
    .Entrada(contador_unos_1_contador), .Convert(convert_display7seg_1_convert));
  BitAdder #(.width(4)) bitadder_1 (.in0(in_6), .out(bitadder_1_out));
  Adder #(.width(3)) adder_1 (
    .a(bitadder_1_out), .b(bitadder_2_out), .out(adder_1_out), .cout(adder_1_cout));  // open: cin
  BitAdder #(.width(4)) bitadder_2 (.in0(in_9), .out(bitadder_2_out));
  BitAdder #(.width(4)) bitadder_3 (.in0(in_11), .out(bitadder_3_out));
  Adder #(.width(3)) adder_2 (
    .a(bitadder_3_out), .b(bitadder_4_out), .out(adder_2_out), .cout(adder_2_cout));  // open: cin
  BitAdder #(.width(4)) bitadder_4 (.in0(in_13), .out(bitadder_4_out));
  BitAdder #(.width(4)) bitadder_5 (.in0(in_15), .out(bitadder_5_out));
  Button button_2 (.out(button_2_out));
  _7_Segment_Display u_7_segment_display_1 (
    .g(convert_display7seg_1_convert[0]), .f(convert_display7seg_1_convert[1]),
    .a(convert_display7seg_1_convert[6]), .b(convert_display7seg_1_convert[5]),
    .e(convert_display7seg_1_convert[2]), .d(convert_display7seg_1_convert[3]),
    .c(convert_display7seg_1_convert[4]));  // open: dp
  assign bit_extender_1_out = {{1{adder_1_cout}}, adder_1_out};  // Bit_Extender bit_extender_1
  assign bit_extender_2_out = {{1{adder_2_cout}}, adder_2_out};  // Bit_Extender bit_extender_2
  Reto1 reto1_1 (.Entrada(in_33), .EN_1(in_41), .EN_2(in_42));
  Adder #(.width(4)) adder_3 (
    .a(bit_extender_1_out), .b(bit_extender_2_out), .out(adder_3_out), .cout(adder_3_cout));  // open: cin
  assign bit_extender_3_out = {{2{1'b0}}, bitadder_5_out};  // Bit_Extender bit_extender_3
  assign bit_extender_4_out = {{1{adder_3_cout}}, adder_3_out};  // Bit_Extender bit_extender_4
  Display_hexa display_hexa_1 (.in_1(in_27));
  // Reto_2 reto_2_1: pin names not known; wires that end beside it: in_35, in_36, in_37
  Adder #(.width(5)) adder_4 (.a(bit_extender_4_out), .b(bit_extender_3_out), .out(out_48));  // open: cin, cout

  assign out_56 = in_20[3:0];
  assign out_57 = in_20[7:4];
  assign out_59 = {in_24, in_26};
  assign out_61 = {in_32, in_31, in_30};

  // Notes on the sheet:
  //   Circuito Seleccionador
  //   Entrada
  //   Circuito Seleccionador de color
  //   Selector
  //   1 0 0
  //   Contador de Unos
  //   Contador de Matriz
endmodule

module Circuito_Elector (
  input  [3:0] A,
  input  SELL,
  input  [3:0] B,
  output [3:0] out_4
);

  wire [3:0] and_1_out, and_2_out, not_1_out;

  assign not_1_out = ~{4{SELL}};  // NOT_Gate not_1, 4 bits wide
  assign and_1_out = A & not_1_out;  // AND_Gate and_1, 4 bits wide
  assign and_2_out = {4{SELL}} & B;  // AND_Gate and_2, 4 bits wide
  assign out_4 = and_1_out | and_2_out;  // OR_Gate or_1, 4 bits wide
endmodule

module Seleccionador_Color (
  input  [2:0] a,
  output [2:0] x
);

  wire and_1_out, and_2_out, and_3_out, and_4_out, and_5_out, and_6_out, and_7_out, and_8_out, and_9_out,
       not_1_out, not_2_out, not_3_out;

  not not_1 (not_1_out, a[2]);
  not not_2 (not_2_out, a[1]);
  not not_3 (not_3_out, a[0]);
  and and_1 (and_1_out, not_1_out, a[0]);
  and and_2 (and_2_out, a[2], not_3_out);
  and and_3 (and_3_out, a[1], a[0]);
  and and_4 (and_4_out, not_2_out, not_3_out);
  and and_5 (and_5_out, a[1], a[0]);
  and and_6 (and_6_out, a[2], not_3_out);
  and and_7 (and_7_out, not_1_out, a[1], not_3_out);
  and and_8 (and_8_out, a[2], not_2_out, not_3_out);
  and and_9 (and_9_out, a[2], a[1], a[0]);
  or or_1 (x[2], and_1_out, and_2_out, and_3_out);
  or or_2 (x[1], and_4_out, and_5_out, and_6_out);
  or or_3 (x[0], and_7_out, and_8_out, and_9_out);
endmodule

module Contador_Unos (
  input  [3:0] Entrada,
  output [2:0] Contador
);

  wire and_2_out, and_3_out, and_4_out, and_5_out, and_6_out, and_7_out, and_8_out, and_9_out, and_10_out,
       and_11_out, and_12_out, and_13_out, and_14_out, and_15_out, not_1_out, not_2_out, not_3_out, not_4_out;

  not not_1 (not_1_out, Entrada[3]);
  not not_2 (not_2_out, Entrada[2]);
  not not_3 (not_3_out, Entrada[1]);
  not not_4 (not_4_out, Entrada[0]);
  and and_1 (Contador[2], Entrada[3], Entrada[2], Entrada[1], Entrada[0]);
  and and_2 (and_2_out, not_1_out, Entrada[1], Entrada[0]);
  and and_3 (and_3_out, not_1_out, Entrada[2], Entrada[0]);
  and and_4 (and_4_out, not_1_out, Entrada[2], Entrada[1]);
  and and_5 (and_5_out, Entrada[3], not_2_out, Entrada[1]);
  and and_6 (and_6_out, Entrada[3], not_3_out, Entrada[0]);
  and and_7 (and_7_out, Entrada[3], Entrada[2], not_4_out);
  and and_8 (and_8_out, not_1_out, not_2_out, not_3_out, Entrada[0]);
  and and_9 (and_9_out, not_1_out, not_2_out, Entrada[1], not_4_out);
  and and_10 (and_10_out, not_1_out, Entrada[2], not_3_out, not_4_out);
  and and_11 (and_11_out, not_1_out, Entrada[2], Entrada[1], Entrada[0]);
  and and_12 (and_12_out, Entrada[3], not_2_out, not_3_out, not_4_out);
  and and_13 (and_13_out, Entrada[3], not_2_out, Entrada[1], Entrada[0]);
  and and_14 (and_14_out, Entrada[3], Entrada[2], not_3_out, Entrada[0]);
  and and_15 (and_15_out, Entrada[3], Entrada[2], Entrada[1], not_4_out);
  or or_1 (Contador[1], and_2_out, and_3_out, and_4_out, and_5_out, and_6_out, and_7_out);
  or or_2 (Contador[0], and_8_out, and_9_out, and_10_out, and_11_out, and_12_out, and_13_out, and_14_out, and_15_out);
endmodule

module Convert_Display7seg (
  input  [2:0] Entrada,
  output [6:0] Convert
);

  wire and_1_out, and_2_out, not_1_out, not_2_out, not_3_out;

  not not_1 (not_1_out, Entrada[2]);
  not not_2 (not_2_out, Entrada[1]);
  not not_3 (not_3_out, Entrada[0]);
  and and_1 (and_1_out, not_1_out, not_3_out);
  or or_1 (Convert[4], not_2_out, Entrada[0]);
  and and_2 (and_2_out, not_1_out, not_3_out);
  and and_3 (Convert[2], not_1_out, not_3_out);
  and and_4 (Convert[1], not_2_out, not_3_out);
  or or_2 (Convert[0], Entrada[1], Entrada[2]);
  or or_3 (Convert[6], and_1_out, Entrada[1]);
  or or_4 (Convert[3], and_2_out, Entrada[1]);

  assign Convert[5] = 1'b1;
endmodule

module Nuevo_Bloque (
  input  Red,
  input  Blue
);

  LED LED1 (.in(Red));
  LED led_1 (.in(Blue));
  LED led_2 (.in(Red));
  LED led_3 (.in(Blue));
  LED led_4 (.in(Red));
  LED led_5 (.in(Blue));
  LED led_6 (.in(Red));
  LED led_7 (.in(Blue));
endmodule

module Display_hexa (
  input  [5:0] in_1
);

  wire [3:0] bit_extender_1_out, bit_extender_1_out_2;

  Hex_Digit_Display hex_digit_display_1 (.value(bit_extender_1_out_2));  // open: dp
  Hex_Digit_Display hex_digit_display_2 (.value(bit_extender_1_out));  // open: dp
  assign {bit_extender_1_out_2, bit_extender_1_out} = {{2{1'b0}}, in_1};  // Bit_Extender bit_extender_1
endmodule

module Logic_Gates (
  input  A,
  input  B
);

  wire and_1_out, not_1_out, not_2_out, or_1_out;

  not not_1 (not_1_out, A);
  LED NOT_A (.in(not_1_out));
  not not_2 (not_2_out, B);
  and and_1 (and_1_out, A, B);
  LED Y (.in(and_1_out));
  or or_1 (or_1_out, A, B);
  LED O (.in(or_1_out));
  LED NOT_B (.in(not_2_out));
endmodule

module Reto1 (
  input  EN_1,
  input  EN_2,
  input  [6:0] Entrada
);

  wire [3:0] and_1_out, and_2_out;
  wire [7:0] bit_extender_1_out;

  Hex_Digit_Display hex_digit_display_1 (.value(and_1_out));  // open: dp
  assign and_1_out = bit_extender_1_out[7:4] & {4{EN_1}};  // AND_Gate and_1, 4 bits wide
  assign bit_extender_1_out = {{1{1'b0}}, Entrada};  // Bit_Extender bit_extender_1
  Hex_Digit_Display hex_digit_display_2 (.value(and_2_out));  // open: dp
  assign and_2_out = bit_extender_1_out[3:0] & {4{EN_2}};  // AND_Gate and_2, 4 bits wide
endmodule

module Reto_2 (
  input  G,
  input  R,
  input  B
);

  // RGBLED rgbled_1: pin names not known; wires that end beside it: R, G, B
endmodule

module Reto_3 (
  input  [7:0] in_1,
  input  [7:0] in_2
);

  wire comparator_1_eq;

  Hex_Digit_Display hex_digit_display_1 (.value(in_1[7:4]));  // open: dp
  Hex_Digit_Display hex_digit_display_2 (.value(in_1[3:0]));  // open: dp
  Hex_Digit_Display hex_digit_display_3 (.value(in_2[7:4]));  // open: dp
  Hex_Digit_Display hex_digit_display_4 (.value(in_2[3:0]));  // open: dp
  Comparator comparator_1 (.a(in_1), .b(in_2), .eq(comparator_1_eq));  // open: gt, lt
  LED led_1 (.in(comparator_1_eq));
endmodule
